// Logisim project Circuit.circ as structural Verilog: 1 circuit, main circuit main
module main (
);

  wire and_1_out, and_2_out, and_3_out, and_4_out, and_5_out, b_out, clock_1_out, not_2_out, not_3_out,
       not_4_out, or_1_out, xor_1_out, xor_2_out;
  wire [2:0] not_1_out, State_q;

  Button b (.out(b_out));
  Register #(.width(3)) State (.D(not_1_out), .Q(State_q), .clk(clock_1_out));  // open: en, clr
  Clock clock_1 (.out(clock_1_out));
  not not_1 (not_1_out[0], b_out);
  not not_2 (not_2_out, State_q[0]);
  not not_3 (not_3_out, State_q[1]);
  not not_4 (not_4_out, State_q[0]);
  LED led_1 (.in(State_q[1]));
  LED led_2 (.in(State_q[2]));
  and and_1 (and_1_out, State_q[1], not_2_out);
  xor xor_1 (xor_1_out, b_out, State_q[1]);
  or or_1 (or_1_out, not_3_out, and_2_out);
  and and_2 (and_2_out, State_q[1], not_4_out);
  xor xor_2 (xor_2_out, State_q[2], b_out);
  and and_3 (and_3_out, State_q[0], xor_1_out);
  and and_4 (and_4_out, State_q[2], or_1_out);
  and and_5 (and_5_out, State_q[0], State_q[1], xor_2_out);
  or or_2 (not_1_out[1], and_1_out, and_3_out);
  or or_3 (not_1_out[2], and_4_out, and_5_out);

  // Notes on the sheet:
  //   r0
  //   r1
  //   r2
  //   s0
  //   s1
  //   n0
  //   n1
  //   n2
endmodule
