// Logisim project 7-segmentModule.circ as structural Verilog: 1 circuit, main circuit 7-segmentModule
module _7_segmentModule (
  input  [3:0] length,
  output s0,
  output s1,
  output s2,
  output s3,
  output s4,
  output s5,
  output s6,
  output s7
);

  wire and_1_out, and_2_out, and_3_out, and_4_out, and_5_out, and_6_out, and_7_out, and_8_out, and_9_out,
       and_10_out, and_11_out, and_12_out, and_13_out, and_14_out, and_15_out, and_16_out, and_17_out,
       and_18_out, and_19_out, and_20_out, and_21_out, and_22_out, and_23_out, and_24_out, and_25_out,
       and_26_out, not_1_out, not_2_out, not_3_out, not_4_out;

  not not_1 (not_1_out, length[2]);
  not not_2 (not_2_out, length[1]);
  not not_3 (not_3_out, length[3]);
  not not_4 (not_4_out, length[0]);
  and and_1 (and_1_out, length[1], not_3_out);
  and and_2 (and_2_out, not_2_out, not_1_out, length[3]);
  and and_3 (and_3_out, length[0], length[2], not_3_out);
  and and_4 (and_4_out, not_4_out, not_1_out, not_3_out);
  and and_5 (and_5_out, not_2_out, not_1_out, length[3]);
  and and_6 (and_6_out, not_2_out, length[2], not_3_out);
  and and_7 (and_7_out, not_4_out, length[2], not_3_out);
  and and_8 (and_8_out, not_4_out, not_2_out, not_3_out);
  and and_9 (and_9_out, not_2_out, not_1_out);
  and and_10 (and_10_out, not_1_out, not_3_out);
  and and_11 (and_11_out, not_4_out, not_2_out, not_3_out);
  and and_12 (and_12_out, length[0], length[1], not_3_out);
  and and_13 (and_13_out, not_2_out, not_1_out, length[3]);
  and and_14 (and_14_out, not_2_out, length[2], not_3_out);
  and and_15 (and_15_out, not_4_out, length[1], not_3_out);
  and and_16 (and_16_out, length[1], not_1_out, not_3_out);
  and and_17 (and_17_out, not_4_out, length[1], not_3_out);
  and and_18 (and_18_out, not_4_out, not_2_out, not_1_out);
  and and_19 (and_19_out, length[2], not_3_out);
  and and_20 (and_20_out, length[0], not_3_out);
  and and_21 (and_21_out, not_2_out, not_1_out);
  and and_22 (and_22_out, not_2_out, not_1_out, length[3]);
  and and_23 (and_23_out, length[1], not_1_out, not_3_out);
  and and_24 (and_24_out, not_4_out, length[1], not_3_out);
  and and_25 (and_25_out, not_4_out, not_1_out, not_3_out);
  and and_26 (and_26_out, length[0], not_2_out, length[2], not_3_out);
  or or_1 (s0, and_1_out, and_2_out, and_3_out, and_4_out);
  or or_2 (s1, and_5_out, and_6_out, and_7_out, and_8_out);
  or or_3 (s2, and_9_out, and_10_out, and_11_out, and_12_out);
  or or_4 (s3, and_13_out, and_14_out, and_15_out, and_16_out);
  or or_5 (s4, and_17_out, and_18_out);
  or or_6 (s5, and_19_out, and_20_out, and_21_out);
  or or_7 (s6, and_22_out, and_23_out, and_24_out, and_25_out, and_26_out);

  assign s7 = 1'b0;
endmodule
