// Logisim project Hangman.circ as structural Verilog: 1 circuit, main circuit Hangman
module Hangman (
  input  a,
  input  b,
  input  c,
  input  [31:0] strfirst32,
  input  [31:0] strlast32,
  input  d,
  input  e,
  input  f,
  input  g,
  input  h,
  input  i,
  input  j,
  input  k,
  input  l,
  input  m,
  input  n,
  input  o,
  input  p,
  input  q,
  input  r,
  input  s,
  input  t,
  input  u,
  input  v,
  input  w,
  input  x,
  input  y,
  input  z,
  input  restart,
  input  go,
  input  goRand,
  input  CLK,
  output s0,
  output s1,
  output out_clr,
  output s2,
  output out_en,
  output s3,
  output [6:0] out,
  output s4,
  output s5,
  output s6,
  output s7,
  output [3:0] win,
  output winPoint,
  output [3:0] lose,
  output losePoint,
  output [15:0] c1,
  output [15:0] c2,
  output [15:0] c3,
  output [15:0] c4,
  output [15:0] c5,
  output [15:0] c6,
  output [15:0] c7,
  output [15:0] c8
);

  wire hangmancontolunit_1_clr, hangmancontolunit_1_err, hangmancontolunit_1_errorl,
       hangmancontolunit_1_errors, hangmancontolunit_1_foundedl, hangmancontolunit_1_foundeds,
       hangmancontolunit_1_foundedstrl, hangmancontolunit_1_foundedstrs, hangmancontolunit_1_gochck,
       hangmancontolunit_1_gol, hangmancontolunit_1_gop, hangmancontolunit_1_inl,
       hangmancontolunit_1_lengthl, hangmancontolunit_1_lengths, hangmancontolunit_1_lose,
       hangmancontolunit_1_ps, hangmancontolunit_1_returnedl, hangmancontolunit_1_returneds,
       hangmancontolunit_1_rl, hangmancontolunit_1_strl, hangmancontolunit_1_strs, hangmancontolunit_1_win,
       inputconverter_1_in, main_1_chckf, main_1_eq0, main_1_eq1, main_1_lenf, main_1_lt, main_1_pf;
  wire [3:0] main_1_length;
  wire [7:0] inputconverter_1_input;

  InputConverter inputconverter_1 (
    .a(a), .b(b), .c(c), .d(d), .e(e), .f(f), .g(g), .h(h), .i(i), .j(j), .k(k), .l(l), .m(m), .n(n), .o(o),
    .p(p), .q(q), .r(r), .s(s), .t(t), .u(u), .v(v), .w(w), .x(x), .y(y), .z(z), .CLK(CLK),
    .in(inputconverter_1_in), .\input (inputconverter_1_input));
  HangmanContolUnit hangmancontolunit_1 (
    .in(inputconverter_1_in), .go(go), .goRand(goRand), .eq0(main_1_eq0), .eq1(main_1_eq1), .lt(main_1_lt),
    .lenF(main_1_lenf), .pF(main_1_pf), .chckF(main_1_chckf), .CLK(CLK), .restart(restart),
    .goL(hangmancontolunit_1_gol), .lengthS(hangmancontolunit_1_lengths),
    .foundedStrL(hangmancontolunit_1_foundedstrl), .lengthL(hangmancontolunit_1_lengthl),
    .err(hangmancontolunit_1_err), .errorS(hangmancontolunit_1_errors), .inL(hangmancontolunit_1_inl),
    .errorL(hangmancontolunit_1_errorl), .goP(hangmancontolunit_1_gop),
    .foundedStrS(hangmancontolunit_1_foundedstrs), .returnedS(hangmancontolunit_1_returneds),
    .pS(hangmancontolunit_1_ps), .goChck(hangmancontolunit_1_gochck),
    .returnedL(hangmancontolunit_1_returnedl), .win(hangmancontolunit_1_win),
    .foundedS(hangmancontolunit_1_foundeds), .lose(hangmancontolunit_1_lose),
    .foundedL(hangmancontolunit_1_foundedl), .CLR(hangmancontolunit_1_clr), .strL(hangmancontolunit_1_strl),
    .strS(hangmancontolunit_1_strs), .rL(hangmancontolunit_1_rl));
  LedModule ledmodule_1 (
    .go(hangmancontolunit_1_err), .CLR(hangmancontolunit_1_clr), .CLK(CLK), .c1(c1), .c2(c2), .c3(c3),
    .c4(c4), .c5(c5), .c6(c6), .c7(c7), .c8(c8));
  HangmanDatapath_main main_1 (
    .pS(hangmancontolunit_1_ps), .rL(hangmancontolunit_1_rl), .strFirst32(strfirst32), .strLast32(strlast32),
    .strS(hangmancontolunit_1_strs), .strL(hangmancontolunit_1_strl),
    .foundedS(hangmancontolunit_1_foundeds), .foundedL(hangmancontolunit_1_foundedl),
    .returnedS(hangmancontolunit_1_returneds), .returnedL(hangmancontolunit_1_returnedl),
    .errorS(hangmancontolunit_1_errors), .errorL(hangmancontolunit_1_errorl),
    .lengthS(hangmancontolunit_1_lengths), .lengthL(hangmancontolunit_1_lengthl),
    .foundedStrS(hangmancontolunit_1_foundedstrs), .foundedStrL(hangmancontolunit_1_foundedstrl), .CLK(CLK),
    .out_clr(out_clr), .lenF(main_1_lenf), .out_en(out_en), .out(out), .lt(main_1_lt), .eq0(main_1_eq0),
    .eq1(main_1_eq1), .goL(hangmancontolunit_1_gol), .goP(hangmancontolunit_1_gop), .pF(main_1_pf),
    .goChck(hangmancontolunit_1_gochck), .chckF(main_1_chckf), .length(main_1_length),
    .\input (inputconverter_1_input), .inL(hangmancontolunit_1_inl), .CLR(hangmancontolunit_1_clr));
  _7_segmentModule u_7_segmentmodule_1 (
    .s0(s0), .s1(s1), .s2(s2), .s3(s3), .s4(s4), .s5(s5), .s6(s6), .s7(s7), .length(main_1_length));
  ScoreModule scoremodule_1 (.in(hangmancontolunit_1_win), .point(winPoint), .score(win));
  ScoreModule scoremodule_2 (.in(hangmancontolunit_1_lose), .point(losePoint), .score(lose));
endmodule
