// Logisim project HangmanControlUnit.circ as structural Verilog: 1 circuit, main circuit HangmanContolUnit
module HangmanContolUnit (
  input  in,
  input  go,
  input  goRand,
  input  eq0,
  input  eq1,
  input  lt,
  input  lenF,
  input  pF,
  input  chckF,
  input  CLK,
  input  restart,
  output goL,
  output lengthS,
  output foundedStrL,
  output lengthL,
  output err,
  output errorS,
  output inL,
  output errorL,
  output goP,
  output foundedStrS,
  output returnedS,
  output pS,
  output goChck,
  output returnedL,
  output win,
  output foundedS,
  output lose,
  output foundedL,
  output CLR,
  output strL,
  output strS,
  output rL
);

  wire and_4_out, and_5_out, and_7_out, and_8_out, and_12_out, and_13_out, and_14_out, and_15_out,
       and_16_out, and_17_out, and_18_out, and_19_out, and_21_out, and_22_out, and_23_out, and_24_out,
       and_25_out, and_26_out, and_27_out, and_28_out, and_29_out, and_31_out, and_32_out, and_38_out,
       and_39_out, and_40_out, and_41_out, and_42_out, and_43_out, and_44_out, and_45_out, and_46_out,
       and_47_out, and_48_out, and_49_out, and_50_out, and_51_out, and_52_out, and_53_out, and_54_out,
       not_1_out, not_2_out, not_3_out, not_4_out, not_5_out, not_6_out, not_7_out, not_8_out, not_9_out,
       not_10_out, not_11_out, xor_1_out;
  wire [3:0] or_8_out, register_1_q;

  not not_1 (not_1_out, go);
  not not_2 (not_2_out, goRand);
  not not_3 (not_3_out, eq0);
  not not_4 (not_4_out, eq1);
  not not_5 (not_5_out, lt);
  not not_6 (not_6_out, pF);
  not not_7 (not_7_out, chckF);
  not not_8 (not_8_out, register_1_q[3]);
  not not_9 (not_9_out, register_1_q[0]);
  not not_10 (not_10_out, register_1_q[2]);
  not not_11 (not_11_out, register_1_q[1]);
  and and_1 (goL, register_1_q[0], register_1_q[1], register_1_q[2], not_8_out);
  and and_2 (lengthL, register_1_q[0], register_1_q[1], not_8_out);
  and and_3 (err, register_1_q[0], not_11_out, register_1_q[2], register_1_q[3]);
  and and_4 (and_4_out, register_1_q[0], not_11_out, register_1_q[2], register_1_q[3]);
  and and_5 (and_5_out, register_1_q[0], register_1_q[1], not_10_out, not_8_out);
  and and_6 (foundedStrS, not_9_out, not_11_out, not_10_out, register_1_q[3]);
  and and_7 (and_7_out, not_9_out, not_11_out, not_10_out, register_1_q[3]);
  and and_8 (and_8_out, register_1_q[0], register_1_q[1], register_1_q[2], register_1_q[3]);
  and and_9 (foundedS, register_1_q[0], register_1_q[1], not_10_out, register_1_q[3]);
  and and_10 (foundedL, register_1_q[0], register_1_q[1], not_10_out);
  xor xor_1 (xor_1_out, register_1_q[0], register_1_q[1]);
  and and_11 (rL, not_9_out, register_1_q[1], not_10_out, not_8_out);
  and and_12 (and_12_out, not_11_out, register_1_q[3]);
  and and_13 (and_13_out, not_10_out, register_1_q[3]);
  and and_14 (and_14_out, not_3_out, not_9_out, register_1_q[3]);
  and and_15 (and_15_out, eq0, register_1_q[0], register_1_q[3]);
  and and_16 (and_16_out, not_6_out, eq0, register_1_q[3]);
  and and_17 (and_17_out, not_5_out, not_3_out, register_1_q[3]);
  and and_18 (and_18_out, in, not_9_out, not_11_out, register_1_q[2]);
  and and_19 (and_19_out, lenF, register_1_q[0], register_1_q[1], register_1_q[2], not_8_out);
  Register #(.width(4)) register_1 (.D(or_8_out), .en(1'b1), .Q(register_1_q), .clk(CLK), .clr(restart));
  or or_1 (errorL, and_4_out, and_5_out);
  or or_2 (returnedL, and_7_out, and_8_out);
  and and_20 (strL, not_10_out, not_8_out, xor_1_out);
  or or_3 (or_8_out[3], and_12_out, and_13_out, and_14_out, and_15_out, and_16_out, and_17_out, and_18_out, and_19_out);
  and and_21 (and_21_out, register_1_q[0], register_1_q[1]);
  and and_22 (and_22_out, register_1_q[0], register_1_q[1]);
  and and_23 (and_23_out, not_7_out, not_11_out, register_1_q[2]);
  and and_24 (and_24_out, not_6_out, register_1_q[1], register_1_q[2]);
  and and_25 (and_25_out, eq0, register_1_q[1], register_1_q[2]);
  and and_26 (and_26_out, register_1_q[2], not_8_out);
  and and_27 (and_27_out, eq1, register_1_q[0], register_1_q[3]);
  and and_28 (and_28_out, not_8_out, not_10_out, register_1_q[1], register_1_q[0]);
  or or_4 (foundedStrL, and_28_out, and_29_out);
  and and_29 (and_29_out, register_1_q[3], not_10_out, not_11_out, not_9_out);
  and and_30 (inL, not_8_out, register_1_q[2], not_11_out, not_9_out);
  and and_31 (and_31_out, register_1_q[3], register_1_q[2], register_1_q[1], not_9_out);
  or or_5 (goP, and_31_out, and_32_out);
  and and_32 (and_32_out, not_8_out, register_1_q[2], not_11_out, register_1_q[0]);
  and and_33 (pS, register_1_q[3], register_1_q[2], register_1_q[1], not_9_out);
  and and_34 (goChck, register_1_q[3], register_1_q[2], not_11_out, not_9_out);
  and and_35 (win, register_1_q[3], not_10_out, register_1_q[1], not_9_out);
  and and_36 (lose, not_8_out, register_1_q[2], register_1_q[1], not_9_out);
  and and_37 (CLR, not_8_out, not_10_out, not_11_out, not_9_out);
  or or_6 (or_8_out[2], and_21_out, and_22_out, and_23_out, and_24_out, and_25_out, and_26_out, and_27_out);
  and and_38 (and_38_out, not_5_out, register_1_q[1]);
  and and_39 (and_39_out, eq0, register_1_q[1]);
  and and_40 (and_40_out, not_9_out, register_1_q[1]);
  and and_41 (and_41_out, not_4_out, register_1_q[0], not_10_out);
  and and_42 (and_42_out, register_1_q[1], not_10_out);
  and and_43 (and_43_out, register_1_q[1], not_8_out);
  and and_44 (and_44_out, goRand, not_1_out, not_10_out, not_8_out);
  and and_45 (and_45_out, register_1_q[0], not_10_out, not_8_out);
  and and_46 (and_46_out, register_1_q[0], not_11_out, register_1_q[2], register_1_q[3]);
  or or_7 (or_8_out[1], and_38_out, and_39_out, and_40_out, and_41_out, and_42_out, and_43_out, and_44_out, and_45_out, and_46_out);
  and and_47 (and_47_out, register_1_q[0], not_10_out);
  and and_48 (and_48_out, not_6_out, register_1_q[0], not_8_out);
  and and_49 (and_49_out, register_1_q[0], register_1_q[1], not_8_out);
  and and_50 (and_50_out, not_2_out, go, not_10_out, not_8_out);
  and and_51 (and_51_out, register_1_q[1], not_10_out, not_8_out);
  and and_52 (and_52_out, lt, not_3_out, register_1_q[0], register_1_q[3]);
  and and_53 (and_53_out, register_1_q[0], not_11_out, register_1_q[3]);
  and and_54 (and_54_out, not_11_out, not_10_out, register_1_q[3]);
  or or_8 (or_8_out[0], and_47_out, and_48_out, and_49_out, and_50_out, and_51_out, and_52_out, and_53_out, and_54_out);

  assign errorS = err;
  assign lengthS = goL;
  assign returnedS = foundedStrS;
  assign strS = rL;
endmodule
