// Logisim project HangmanDatapath.circ as structural Verilog: 1 circuit, main circuit main
module main (
  input  pS,
  input  goP,
  input  rL,
  input  goChck,
  input  goL,
  input  [31:0] strFirst32,
  input  [31:0] strLast32,
  input  strS,
  input  strL,
  input  foundedS,
  input  foundedL,
  input  returnedS,
  input  returnedL,
  input  errorS,
  input  errorL,
  input  lengthS,
  input  lengthL,
  input  [7:0] \input ,
  input  inL,
  input  CLR,
  input  foundedStrS,
  input  foundedStrL,
  input  CLK,
  output pF,
  output chckF,
  output out_clr,
  output lenF,
  output out_en,
  output [6:0] out,
  output lt,
  output eq0,
  output eq1,
  output [3:0] length
);

  wire [3:0] adder_1_out, adder_2_out, error_q, founded_q, inputchecker_1_returned, lengthmodule_1_length,
       multiplexer_3_out, multiplexer_4_out, multiplexer_5_out, multiplexer_6_out, returned_q;
  wire [6:0] random_1_out;
  wire [7:0] input_q;
  wire [31:0] foundedFirst32_q, foundedLast32_q, inputchecker_1_foundedf32bit, inputchecker_1_foundedl32bit,
       multiplexer_1_out, multiplexer_2_out, multiplexer_7_out, multiplexer_8_out, multiplexer_9_out,
       multiplexer_10_out, rom_1_data, rom_2_data, strFirst32_q, strLast32_q;

  Random #(.width(7)) random_1 (.clk(CLK), .next(rL), .out(random_1_out), .clr(1'b0));
  ROM #(.addrWidth(7), .dataWidth(32)) rom_1 (.addr(random_1_out), .data(rom_1_data), .sel(1'b1));
  ROM #(.addrWidth(7), .dataWidth(32)) rom_2 (.addr(random_1_out), .data(rom_2_data), .sel(1'b1));
  Multiplexer #(.width(32), .enable("false")) multiplexer_1 (
    .in0(strFirst32), .in1(rom_1_data), .out(multiplexer_1_out), .sel(strS));
  Multiplexer #(.width(32), .enable("false")) multiplexer_2 (
    .in0(strLast32), .in1(rom_2_data), .out(multiplexer_2_out), .sel(strS));
  Multiplexer #(.width(4), .enable("false")) multiplexer_3 (
    .in0(4'b0000), .in1(adder_1_out), .out(multiplexer_3_out), .sel(foundedS));
  Multiplexer #(.width(4), .enable("false")) multiplexer_4 (
    .in0(4'b0000), .in1(inputchecker_1_returned), .out(multiplexer_4_out), .sel(returnedS));
  Multiplexer #(.width(4), .enable("false")) multiplexer_5 (
    .in0(4'b0000), .in1(adder_2_out), .out(multiplexer_5_out), .sel(errorS));
  Multiplexer #(.width(4), .enable("false")) multiplexer_6 (
    .in0(4'b0000), .in1(lengthmodule_1_length), .out(multiplexer_6_out), .sel(lengthS));
  Multiplexer #(.width(32), .enable("false")) multiplexer_7 (
    .in0(32'h5f5f5f5f), .in1(inputchecker_1_foundedf32bit), .out(multiplexer_7_out), .sel(foundedStrS));
  Multiplexer #(.width(32), .enable("false")) multiplexer_8 (
    .in0(32'h5f5f5f5f), .in1(inputchecker_1_foundedl32bit), .out(multiplexer_8_out), .sel(foundedStrS));
  Register #(.width(32)) u_strFirst32 (.D(multiplexer_1_out), .en(strL), .Q(strFirst32_q), .clk(CLK), .clr(CLR));
  Register #(.width(32)) u_strLast32 (.D(multiplexer_2_out), .en(strL), .Q(strLast32_q), .clk(CLK), .clr(CLR));
  Register #(.width(4)) founded (.D(multiplexer_3_out), .en(foundedL), .Q(founded_q), .clk(CLK), .clr(CLR));
  Register #(.width(4)) returned (.D(multiplexer_4_out), .en(returnedL), .Q(returned_q), .clk(CLK), .clr(CLR));
  Register #(.width(4)) error (.D(multiplexer_5_out), .en(errorL), .Q(error_q), .clk(CLK), .clr(CLR));
  Register #(.width(4)) u_length (.D(multiplexer_6_out), .en(lengthL), .Q(length), .clk(CLK), .clr(CLR));
  Register u_input (.D(\input ), .en(inL), .Q(input_q), .clk(CLK), .clr(CLR));
  Register #(.width(32)) foundedFirst32 (
    .D(multiplexer_7_out), .en(foundedStrL), .Q(foundedFirst32_q), .clk(CLK), .clr(CLR));
  Register #(.width(32)) foundedLast32 (
    .D(multiplexer_8_out), .en(foundedStrL), .Q(foundedLast32_q), .clk(CLK), .clr(CLR));
  LengthModule lengthmodule_1 (
    .strfirst32(strFirst32_q), .go(goL), .CLR(CLR), .CLK(CLK), .strlast32(strLast32_q), .finish(lenF),
    .length(lengthmodule_1_length));
  Adder #(.width(4)) adder_1 (.a(founded_q), .b(returned_q), .out(adder_1_out), .cin(1'b0));  // open: cout
  Adder #(.width(4)) adder_2 (.a(error_q), .b(4'b0001), .out(adder_2_out), .cin(1'b0));  // open: cout
  Multiplexer #(.width(32), .enable("false")) multiplexer_9 (
    .in0(foundedFirst32_q), .in1(strFirst32_q), .out(multiplexer_9_out), .sel(pS));
  Multiplexer #(.width(32), .enable("false")) multiplexer_10 (
    .in0(foundedLast32_q), .in1(strLast32_q), .out(multiplexer_10_out), .sel(pS));
  Printer printer_1 (
    .out(out), .out_en(out_en), .out_clr(out_clr), .finish(pF), .CLK(CLK), .go(goP),
    .first32bit(multiplexer_9_out), .last32bit(multiplexer_10_out), .length(length), .CLR(CLR));
  Comparator #(.width(4), .mode("unsigned")) comparator_1 (.a(founded_q), .b(length), .lt(lt));  // open: gt, eq
  Comparator #(.width(4), .mode("unsigned")) comparator_2 (.a(error_q), .b(4'b1010), .eq(eq0));  // open: gt, lt
  Comparator #(.width(4), .mode("unsigned")) comparator_3 (.a(returned_q), .b(4'b0000), .eq(eq1));  // open: gt, lt
  InputChecker inputchecker_1 (
    .go(goChck), .first32bit(strFirst32_q), .last32bit(strLast32_q),
    .foundedf32bit(inputchecker_1_foundedf32bit), .foundedl32bit(inputchecker_1_foundedl32bit),
    .returned(inputchecker_1_returned), .foundedlast32bit(foundedLast32_q),
    .foundedfirst32bit(foundedFirst32_q), .finish(chckF), .length(length), .\input (input_q), .CLK(CLK));

  // Notes on the sheet:
  //   contents of rom_1 (hex, n*v repeats v):
  //   68 63616d70 696d 646973 6465 6761 637275 6d61 0 67726164 70726f 6d75 72 0 73 0 6e7563 0 63 6f62
  //   616d6269 77 7468 64656372 0 696e6469 706f 73 6272 0 0 7361 0 616e 73656e74 64 656d 0 70726f 7175
  //   706174 736361 0 6361 0 696e 666963 0 706c 0 0 74 636f6d 0 73 6368 6368 70 6c6f 6d 6661 67 64656369 0
  //   636869 736572 64 7465 70 0 0 6d757461 737475 0 66 74726961 0 736b 647261 0 6275 0 73746f 0 73 6f
  //   636f6d6d 74 6d75 7265 74 7379 666c 70726f73 70 6761 74 7375 67 66 0 0 0 726576 63 73 0 70726163 71
  //   666169 6775 64656e 0 0 0 6d6f 6f 0 7265 0 0 70726f66 0 0 0 73616e64 7375 6d7573
  //   contents of rom_2 (hex, n*v repeats v):
  //   656c6c6f 6169676e 70616374 63757373 63616465 726c6963 73616465 72626c65 626f6d62 69656e74 6d6f7465
  //   7475616c 6f756768 686974 68656c6c 686974 6c656172 72756e67 726f7373 6a656374 74696f6e 726f6e67
  //   616e6b73 65617365 7661696e 72656374 6c697465 706f7274 6f6e7a65 73686564 746f6e 696c6f72 7065616b
  //   696d616c 656e6365 72696674 70697265 636172 63657373 61696e74 7465726e 6e64616c 72656172 6e766173
  //   6d696c6c 73657274 74696f6e 73746570 61796572 62757368 73616e64 68656674 70616e79 74657874 63726577
  //   65657365 65717565 72696465 756e6765 65726974 766f7572 72656174 73697665 736f6674 6d6e6579 696f7573
  //   72616d61 6d706c65 61696e74 68617465 676170 74696f6e 6d626c65 6c656166 696e616c 6e676c65 62726167
  //   65746368 77696e67 6e657773 64676574 62656172 72616765 65617374 74616b65 62657365 65726365 77697374
  //   72646572 70656174 68696768 6d626f6c 61776564 70656374 696c6f74 72616765 69676572 72766579 6c696465
  //   72657368 66616365 74727565 6465616c 656e6765 6f616368 6c696465 706f7374 74696365 7565656e 6c757265
  //   74746572 74697374 626f79 736c616d 737079 73717565 72646572 676f64 61646572 70617274 70757265
  //   6f756e64 6368696e 70696c65 6b6e6565 77696368 6d6d6572 6963616c
endmodule
