// Logisim project InputChecker.circ as structural Verilog: 1 circuit, main circuit InputChecker
module InputChecker (
  input  [31:0] first32bit,
  input  [31:0] last32bit,
  input  go,
  input  [3:0] length,
  input  [7:0] \input ,
  input  CLK,
  input  [31:0] foundedfirst32bit,
  input  [31:0] foundedlast32bit,
  output [31:0] foundedf32bit,
  output [31:0] foundedl32bit,
  output finish,
  output [3:0] returned
);

  wire inputcheckerconrtolunit_1_as, inputcheckerconrtolunit_1_cs, inputcheckerconrtolunit_1_den,
       inputcheckerconrtolunit_1_li, inputcheckerconrtolunit_1_lr, inputcheckerconrtolunit_1_op,
       inputcheckerconrtolunit_1_si, inputcheckerconrtolunit_1_sr, inputcheckerdatapath_1_feq,
       inputcheckerdatapath_1_lt, inputcheckerdatapath_1_streq;

  InputCheckerConrtolUnit inputcheckerconrtolunit_1 (
    .fEq(inputcheckerdatapath_1_feq), .strEq(inputcheckerdatapath_1_streq), .go(go),
    .lt(inputcheckerdatapath_1_lt), .finish(finish), .op(inputcheckerconrtolunit_1_op),
    .den(inputcheckerconrtolunit_1_den), .as(inputcheckerconrtolunit_1_as),
    .cs(inputcheckerconrtolunit_1_cs), .sr(inputcheckerconrtolunit_1_sr), .lr(inputcheckerconrtolunit_1_lr),
    .si(inputcheckerconrtolunit_1_si), .li(inputcheckerconrtolunit_1_li), .CLK(CLK));
  InputCheckerDatapath inputcheckerdatapath_1 (
    .length(length), .\input (\input ), .cs(inputcheckerconrtolunit_1_cs), .si(inputcheckerconrtolunit_1_si),
    .li(inputcheckerconrtolunit_1_li), .foundedlast32bit(foundedlast32bit),
    .sr(inputcheckerconrtolunit_1_sr), .lr(inputcheckerconrtolunit_1_lr), .CLK(CLK),
    .foundedfirst32bit(foundedfirst32bit), .last32bit(last32bit), .first32bit(first32bit),
    .strEq(inputcheckerdatapath_1_streq), .lt(inputcheckerdatapath_1_lt), .foundedl32bit(foundedl32bit),
    .foundedf32bit(foundedf32bit), .as(inputcheckerconrtolunit_1_as), .den(inputcheckerconrtolunit_1_den),
    .op(inputcheckerconrtolunit_1_op), .returned(returned), .fEq(inputcheckerdatapath_1_feq));
endmodule
