// Logisim project InputCheckerControlUnit.circ as structural Verilog: 1 circuit, main circuit InputCheckerConrtolUnit
module InputCheckerConrtolUnit (
  input  fEq,
  input  strEq,
  input  go,
  input  lt,
  input  CLK,
  output finish,
  output op,
  output den,
  output as,
  output cs,
  output sr,
  output lr,
  output si,
  output li
);

  wire and_9_out, and_10_out, and_11_out, and_12_out, and_13_out, and_14_out, and_15_out, and_16_out,
       and_17_out, not_1_out, not_2_out, not_3_out, not_4_out, not_5_out, xor_1_out;
  wire [2:0] or_1_out, register_1_q;

  not not_1 (not_1_out, lt);
  not not_2 (not_2_out, strEq);
  not not_3 (not_3_out, register_1_q[2]);
  not not_4 (not_4_out, register_1_q[0]);
  not not_5 (not_5_out, register_1_q[1]);
  Register #(.width(3)) register_1 (.D(or_1_out), .en(1'b1), .Q(register_1_q), .clk(CLK), .clr(1'b0));
  and and_1 (finish, not_1_out, not_4_out, register_1_q[1], not_3_out);
  and and_2 (op, register_1_q[0], not_5_out, not_3_out);
  and and_3 (as, not_4_out, not_5_out, register_1_q[2]);
  and and_4 (cs, register_1_q[0], register_1_q[1], not_3_out);
  and and_5 (sr, not_4_out, not_5_out, register_1_q[2]);
  and and_6 (lr, not_5_out, xor_1_out);
  xor xor_1 (xor_1_out, register_1_q[0], register_1_q[2]);
  and and_7 (si, register_1_q[0], not_5_out, register_1_q[2]);
  and and_8 (li, register_1_q[0], not_5_out);
  and and_9 (and_9_out, not_4_out, not_5_out, register_1_q[2]);
  and and_10 (and_10_out, fEq, register_1_q[0], register_1_q[1], not_3_out);
  or or_1 (or_1_out[0], and_9_out, and_10_out, and_11_out, and_12_out, and_13_out);
  and and_11 (and_11_out, not_2_out, register_1_q[0], register_1_q[1], not_3_out);
  and and_12 (and_12_out, lt, not_4_out, register_1_q[1], not_3_out);
  and and_13 (and_13_out, go, not_4_out, not_5_out, not_3_out);
  and and_14 (and_14_out, lt, not_4_out, register_1_q[1], not_3_out);
  or or_2 (or_1_out[1], and_14_out, and_15_out);
  and and_15 (and_15_out, register_1_q[0], not_5_out);
  and and_16 (and_16_out, not_4_out, not_5_out, register_1_q[2]);
  or or_3 (or_1_out[2], and_16_out, and_17_out);
  and and_17 (and_17_out, register_1_q[0], register_1_q[1], not_3_out);

  assign den = as;
endmodule
