// Logisim project InputCheckerDatapath.circ as structural Verilog: 1 circuit, main circuit InputCheckerDatapath
module InputCheckerDatapath (
  input  den,
  input  op,
  input  [3:0] length,
  input  [7:0] \input ,
  input  cs,
  input  si,
  input  li,
  input  as,
  input  [31:0] foundedlast32bit,
  input  sr,
  input  lr,
  input  CLK,
  input  [31:0] foundedfirst32bit,
  input  [31:0] last32bit,
  input  [31:0] first32bit,
  output strEq,
  output lt,
  output [3:0] returned,
  output [31:0] foundedl32bit,
  output [31:0] foundedf32bit,
  output fEq
);

  wire decoder_1_out0, decoder_1_out1, decoder_1_out2, decoder_1_out3, decoder_1_out4, decoder_1_out5,
       decoder_1_out6, decoder_1_out7, multiplexer_17_out, multiplexer_18_out, multiplexer_19_out,
       multiplexer_20_out, multiplexer_21_out, multiplexer_22_out, multiplexer_23_out, multiplexer_24_out;
  wire [2:0] bit_extender_3_out;
  wire [3:0] adder_1_out, i_q, multiplexer_1_out, multiplexer_2_out, multiplexer_6_out, multiplexer_8_out;
  wire [7:0] bit_extender_1_out, bit_extender_2_out, multiplexer_3_out, multiplexer_4_out, multiplexer_5_out,
       multiplexer_7_out, multiplexer_9_out, multiplexer_10_out, multiplexer_11_out, multiplexer_12_out,
       multiplexer_13_out, multiplexer_14_out, multiplexer_15_out, multiplexer_16_out;

  assign bit_extender_1_out = {{4{1'b0}}, length};  // Bit_Extender bit_extender_1
  Multiplexer #(.width(4), .enable("false")) multiplexer_1 (
    .in0(4'b0000), .in1(adder_1_out), .out(multiplexer_1_out), .sel(si));
  Register #(.width(4)) i (.D(multiplexer_1_out), .en(li), .Q(i_q), .clk(CLK), .clr(1'b0));
  Multiplexer #(.width(4), .enable("false")) multiplexer_2 (
    .in0(4'b0000), .in1(adder_1_out), .out(multiplexer_2_out), .sel(sr));
  Register #(.width(4)) u_returned (.D(multiplexer_2_out), .en(lr), .Q(returned), .clk(CLK), .clr(1'b0));
  assign bit_extender_2_out = {{4{1'b0}}, i_q};  // Bit_Extender bit_extender_2
  Multiplexer #(.select(3), .width(8), .enable("false")) multiplexer_3 (
    .in0(last32bit[7:0]), .in1(last32bit[15:8]), .in2(last32bit[23:16]), .in3(last32bit[31:24]),
    .in4(first32bit[7:0]), .in5(first32bit[15:8]), .in6(first32bit[23:16]), .in7(first32bit[31:24]),
    .out(multiplexer_3_out), .sel(bit_extender_3_out));
  Bit_Extender #(.in_width(4), .out_width(3)) bit_extender_3 (.in(i_q), .out(bit_extender_3_out));
  Multiplexer #(.width(8), .enable("false")) multiplexer_4 (
    .in0(bit_extender_2_out), .in1(\input ), .out(multiplexer_4_out), .sel(cs));
  Multiplexer #(.width(8), .enable("false")) multiplexer_5 (
    .in0(bit_extender_1_out), .in1(multiplexer_3_out), .out(multiplexer_5_out), .sel(cs));
  Multiplexer #(.width(4), .enable("false")) multiplexer_6 (
    .in0(i_q), .in1(returned), .out(multiplexer_6_out), .sel(as));
  Comparator comparator_1 (.a(multiplexer_4_out), .b(multiplexer_5_out), .eq(strEq), .lt(lt));  // open: gt
  Adder #(.width(4)) adder_1 (.a(multiplexer_6_out), .b(4'b0001), .out(adder_1_out));  // open: cin, cout
  Comparator comparator_2 (.a(multiplexer_7_out), .b(\input ), .eq(fEq));  // open: gt, lt
  Multiplexer #(.select(3), .width(8), .enable("false")) multiplexer_7 (
    .in0(foundedlast32bit[7:0]), .in1(foundedlast32bit[15:8]), .in2(foundedlast32bit[23:16]),
    .in3(foundedlast32bit[31:24]), .in4(foundedfirst32bit[7:0]), .in5(foundedfirst32bit[15:8]),
    .in6(foundedfirst32bit[23:16]), .in7(foundedfirst32bit[31:24]), .out(multiplexer_7_out),
    .sel(bit_extender_3_out));
  Multiplexer #(.width(4), .enable("false")) multiplexer_8 (
    .in0(4'b1000), .in1(i_q), .out(multiplexer_8_out), .sel(den));
  Multiplexer #(.width(8), .enable("false")) multiplexer_9 (
    .in0(foundedlast32bit[7:0]), .in1(\input ), .out(multiplexer_9_out), .sel(decoder_1_out0));
  Multiplexer #(.width(8), .enable("false")) multiplexer_10 (
    .in0(foundedlast32bit[15:8]), .in1(\input ), .out(multiplexer_10_out), .sel(decoder_1_out1));
  Multiplexer #(.width(8), .enable("false")) multiplexer_11 (
    .in0(foundedlast32bit[23:16]), .in1(\input ), .out(multiplexer_11_out), .sel(decoder_1_out2));
  Multiplexer #(.width(8), .enable("false")) multiplexer_12 (
    .in0(foundedlast32bit[31:24]), .in1(\input ), .out(multiplexer_12_out), .sel(decoder_1_out3));
  Multiplexer #(.width(8), .enable("false")) multiplexer_13 (
    .in0(foundedfirst32bit[7:0]), .in1(\input ), .out(multiplexer_13_out), .sel(decoder_1_out4));
  Multiplexer #(.width(8), .enable("false")) multiplexer_14 (
    .in0(foundedfirst32bit[15:8]), .in1(\input ), .out(multiplexer_14_out), .sel(decoder_1_out5));
  Multiplexer #(.width(8), .enable("false")) multiplexer_15 (
    .in0(foundedfirst32bit[23:16]), .in1(\input ), .out(multiplexer_15_out), .sel(decoder_1_out6));
  Multiplexer #(.width(8), .enable("false")) multiplexer_16 (
    .in0(foundedfirst32bit[31:24]), .in1(\input ), .out(multiplexer_16_out), .sel(decoder_1_out7));
  Multiplexer #(.enable("false")) multiplexer_17 (.in0(decoder_1_out0), .in1(1'b1), .out(multiplexer_17_out), .sel(op));
  Multiplexer #(.enable("false")) multiplexer_18 (.in0(decoder_1_out1), .in1(1'b1), .out(multiplexer_18_out), .sel(op));
  Multiplexer #(.enable("false")) multiplexer_19 (.in0(decoder_1_out2), .in1(1'b1), .out(multiplexer_19_out), .sel(op));
  Multiplexer #(.enable("false")) multiplexer_20 (.in0(decoder_1_out3), .in1(1'b1), .out(multiplexer_20_out), .sel(op));
  Multiplexer #(.enable("false")) multiplexer_21 (.in0(decoder_1_out4), .in1(1'b1), .out(multiplexer_21_out), .sel(op));
  Multiplexer #(.enable("false")) multiplexer_22 (.in0(decoder_1_out5), .in1(1'b1), .out(multiplexer_22_out), .sel(op));
  Multiplexer #(.enable("false")) multiplexer_23 (.in0(decoder_1_out6), .in1(1'b1), .out(multiplexer_23_out), .sel(op));
  Multiplexer #(.enable("false")) multiplexer_24 (.in0(decoder_1_out7), .in1(1'b1), .out(multiplexer_24_out), .sel(op));
  Decoder #(.select(4), .enable("false")) decoder_1 (
    .out0(decoder_1_out0), .out1(decoder_1_out1), .out2(decoder_1_out2), .out3(decoder_1_out3),
    .out4(decoder_1_out4), .out5(decoder_1_out5), .out6(decoder_1_out6), .out7(decoder_1_out7),
    .sel(multiplexer_8_out));  // open: out8, out9, out10, out11, out12, out13, out14, out15
  Register register_1 (.D(multiplexer_9_out), .en(multiplexer_17_out), .Q(foundedl32bit[7:0]), .clk(CLK), .clr(1'b0));
  Register register_2 (.D(multiplexer_10_out), .en(multiplexer_18_out), .Q(foundedl32bit[15:8]), .clk(CLK), .clr(1'b0));
  Register register_3 (
    .D(multiplexer_11_out), .en(multiplexer_19_out), .Q(foundedl32bit[23:16]), .clk(CLK), .clr(1'b0));
  Register register_4 (
    .D(multiplexer_12_out), .en(multiplexer_20_out), .Q(foundedl32bit[31:24]), .clk(CLK), .clr(1'b0));
  Register register_5 (.D(multiplexer_13_out), .en(multiplexer_21_out), .Q(foundedf32bit[7:0]), .clk(CLK), .clr(1'b0));
  Register register_6 (.D(multiplexer_14_out), .en(multiplexer_22_out), .Q(foundedf32bit[15:8]), .clk(CLK), .clr(1'b0));
  Register register_7 (
    .D(multiplexer_15_out), .en(multiplexer_23_out), .Q(foundedf32bit[23:16]), .clk(CLK), .clr(1'b0));
  Register register_8 (
    .D(multiplexer_16_out), .en(multiplexer_24_out), .Q(foundedf32bit[31:24]), .clk(CLK), .clr(1'b0));
endmodule
