// Logisim project InputConverter.circ as structural Verilog: 1 circuit, main circuit InputConverter
module InputConverter (
  input  a,
  input  b,
  input  c,
  input  d,
  input  e,
  input  f,
  input  g,
  input  h,
  input  i,
  input  j,
  input  CLK,
  input  k,
  input  l,
  input  m,
  input  n,
  input  o,
  input  p,
  input  q,
  input  r,
  input  s,
  input  t,
  input  u,
  input  v,
  input  w,
  input  x,
  input  y,
  input  z,
  output in,
  output [7:0] \input 
);

  wire or_1_out;

  Priority_Encoder #(.select(5)) priority_encoder_1 (
    .in0(1'b1), .in1(a), .in2(b), .in3(c), .in4(d), .in5(e), .in6(f), .in7(g), .in8(h), .in9(i), .in10(j),
    .in11(k), .in12(l), .in13(m), .in14(n), .in15(o), .in16(p), .in17(q), .in18(r), .in19(s), .in20(t),
    .in21(u), .in22(v), .in23(w), .in24(x), .in25(y), .in26(z), .in27(1'b0), .in28(1'b0), .in29(1'b0),
    .in30(1'b0), .in31(1'b0), .out(\input [4:0]), .en_in(1'b1));  // open: gs, en_out
  Button_Syncronizer button_syncronizer_1 (.in(or_1_out), .CLK(CLK), .out(in));
  or or_1 (or_1_out, \input [0], \input [1], \input [2], \input [3], \input [4]);

  assign \input [7:5] = 3'b011;
endmodule
