// Logisim project LedModule.circ as structural Verilog: 1 circuit, main circuit LedModule
module LedModule (
  input  go,
  input  CLR,
  input  CLK,
  output [15:0] c1,
  output [15:0] c2,
  output [15:0] c3,
  output [15:0] c4,
  output [15:0] c5,
  output [15:0] c6,
  output [15:0] c7,
  output [15:0] c8
);

  wire ledmodulecontrolunit_1_li, ledmodulecontrolunit_1_si, ledmoduledatapath_1_gt;

  LedModuleControlUnit ledmodulecontrolunit_1 (
    .go(go), .gt(ledmoduledatapath_1_gt), .CLK(CLK), .CLR(CLR), .si(ledmodulecontrolunit_1_si),
    .li(ledmodulecontrolunit_1_li));
  LedModuleDataPath ledmoduledatapath_1 (
    .c1(c1), .c2(c2), .c3(c3), .c4(c4), .c5(c5), .c6(c6), .c7(c7), .c8(c8), .si(ledmodulecontrolunit_1_si),
    .li(ledmodulecontrolunit_1_li), .CLK(CLK), .gt(ledmoduledatapath_1_gt));
endmodule
