// Logisim project LedModuleControlUnit.circ as structural Verilog: 1 circuit, main circuit LedModuleControlUnit
module LedModuleControlUnit (
  input  go,
  input  gt,
  input  CLK,
  input  CLR,
  output si,
  output li
);

  wire and_1_out, and_2_out, and_3_out, and_4_out, and_5_out, not_1_out, not_2_out, not_3_out, not_4_out;
  wire [1:0] or_2_out;
  wire [1:1] register_1_q;

  not not_1 (not_1_out, go);
  not not_2 (not_2_out, gt);
  not not_3 (not_3_out, register_1_q[1]);
  not not_4 (not_4_out, si);
  and and_1 (and_1_out, not_4_out, not_3_out);
  and and_2 (and_2_out, not_2_out, go, not_4_out);
  and and_3 (and_3_out, go, not_4_out, not_3_out);
  and and_4 (and_4_out, not_1_out, not_4_out, register_1_q[1]);
  and and_5 (and_5_out, not_2_out, not_4_out, register_1_q[1]);
  Register #(.width(2)) register_1 (.D(or_2_out), .en(1'b1), .Q({register_1_q[1], si}), .clk(CLK), .clr(CLR));
  or or_1 (li, and_1_out, si);
  or or_2 (or_2_out[0], and_2_out, and_3_out);
  or or_3 (or_2_out[1], and_4_out, and_5_out, si);
endmodule
