// Logisim project LedModuleDatapath.circ as structural Verilog: 1 circuit, main circuit LedModuleDataPath
module LedModuleDataPath (
  input  si,
  input  li,
  input  CLK,
  output gt,
  output [15:0] c1,
  output [15:0] c2,
  output [15:0] c3,
  output [15:0] c4,
  output [15:0] c5,
  output [15:0] c6,
  output [15:0] c7,
  output [15:0] c8
);

  wire [3:0] adder_1_out, i_q, multiplexer_1_out;

  Register #(.width(4)) i (.D(multiplexer_1_out), .en(li), .Q(i_q), .clk(CLK));  // open: clr
  Multiplexer #(.width(4), .enable("false")) multiplexer_1 (
    .in0(4'b0000), .in1(adder_1_out), .out(multiplexer_1_out), .sel(si));
  Multiplexer #(.select(4), .width(16), .enable("false")) multiplexer_2 (
    .in0({16{1'b0}}), .in1(16'h1), .in2(16'h1), .in3(16'h1), .in4(16'h1), .in5(16'h1), .in6(16'h1),
    .in7(16'h1), .in8(16'h1), .in9(16'h1), .in10(16'h1), .out(c1), .sel(i_q));  // open: in11, in12, in13, in14, in15
  Adder #(.width(4)) adder_1 (.a(i_q), .b(4'b0001), .out(adder_1_out));  // open: cin, cout
  Comparator #(.width(4), .mode("unsigned")) comparator_1 (.a(i_q), .b(4'b1001), .gt(gt));  // open: eq, lt
  Multiplexer #(.select(4), .width(16), .enable("false")) multiplexer_3 (
    .in0({16{1'b0}}), .in1(16'h1), .in2({16{1'b1}}), .in3({16{1'b1}}), .in4({16{1'b1}}), .in5({16{1'b1}}),
    .in6({16{1'b1}}), .in7({16{1'b1}}), .in8({16{1'b1}}), .in9({16{1'b1}}), .in10({16{1'b1}}), .out(c2),
    .sel(i_q));  // open: in11, in12, in13, in14, in15
  Multiplexer #(.select(4), .width(16), .enable("false")) multiplexer_4 (
    .in0({16{1'b0}}), .in1(16'h1), .in2(16'h1), .in3(16'h8001), .in4(16'h8001), .in5(16'h8001),
    .in6(16'h8001), .in7(16'h8001), .in8(16'h8001), .in9(16'h8001), .in10(16'h8001), .out(c3), .sel(i_q));  // open: in11, in12, in13, in14, in15
  Multiplexer #(.select(4), .width(16), .enable("false")) multiplexer_5 (
    .in0({16{1'b0}}), .in1(16'h1), .in2(16'h1), .in3(16'h8001), .in4(16'h8001), .in5(16'h8c01),
    .in6(16'h8c01), .in7(16'h8c41), .in8(16'h8c41), .in9(16'h8c4d), .in10(16'h8c4d), .out(c4), .sel(i_q));  // open: in11, in12, in13, in14, in15
  Multiplexer #(.select(4), .width(16), .enable("false")) multiplexer_6 (
    .in0({16{1'b0}}), .in1(16'h1), .in2(16'h1), .in3(16'h8001), .in4(16'h8001), .in5(16'h9201),
    .in6(16'h9201), .in7(16'h9281), .in8(16'h9281), .in9(16'h9291), .in10(16'h9291), .out(c5), .sel(i_q));  // open: in11, in12, in13, in14, in15
  Multiplexer #(.select(4), .width(16), .enable("false")) multiplexer_7 (
    .in0({16{1'b0}}), .in1({16{1'b0}}), .in2({16{1'b0}}), .in3(16'h8000), .in4(16'he000), .in5(16'hf200),
    .in6(16'hf3e0), .in7(16'hf3e0), .in8(16'hf3e0), .in9(16'hf3e0), .in10(16'hf3e0), .out(c6), .sel(i_q));  // open: in11, in12, in13, in14, in15
  Multiplexer #(.select(4), .width(16), .enable("false")) multiplexer_8 (
    .in0({16{1'b0}}), .in1({16{1'b0}}), .in2({16{1'b0}}), .in3({16{1'b0}}), .in4({16{1'b0}}), .in5(16'h1200),
    .in6(16'h1200), .in7(16'h1200), .in8(16'h1280), .in9(16'h1280), .in10(16'h1290), .out(c7), .sel(i_q));  // open: in11, in12, in13, in14, in15
  Multiplexer #(.select(4), .width(16), .enable("false")) multiplexer_9 (
    .in0({16{1'b0}}), .in1({16{1'b0}}), .in2({16{1'b0}}), .in3({16{1'b0}}), .in4({16{1'b0}}), .in5(16'hc00),
    .in6(16'hc00), .in7(16'hc00), .in8(16'hc40), .in9(16'hc40), .in10(16'hc4c), .out(c8), .sel(i_q));  // open: in11, in12, in13, in14, in15
endmodule
