// Logisim project LengthModule.circ as structural Verilog: 1 circuit, main circuit LengthModule
module LengthModule (
  input  [31:0] strfirst32,
  input  [31:0] strlast32,
  input  go,
  input  CLR,
  input  CLK,
  output finish,
  output [3:0] length
);

  wire lengthmodulecontolunit_1_loadl, lengthmodulecontolunit_1_loadstr, lengthmodulecontolunit_1_selectl,
       lengthmoduledatapath_1_eq;
  wire [3:0] lengthmoduledatapath_1_len;

  LengthModuleContolUnit lengthmodulecontolunit_1 (
    .eq(lengthmoduledatapath_1_eq), .finish(finish), .loadStr(lengthmodulecontolunit_1_loadstr),
    .selectL(lengthmodulecontolunit_1_selectl), .loadL(lengthmodulecontolunit_1_loadl), .go(go), .CLK(CLK),
    .CLR(CLR), .len(lengthmoduledatapath_1_len), .length(length));
  LengthModuleDatapath lengthmoduledatapath_1 (
    .selectL(lengthmodulecontolunit_1_selectl), .loadL(lengthmodulecontolunit_1_loadl), .CLK(CLK), .CLR(CLR),
    .loadStr(lengthmodulecontolunit_1_loadstr), .str_in_Last32(strlast32), .str_in_First32(strfirst32),
    .eq(lengthmoduledatapath_1_eq), .len(lengthmoduledatapath_1_len));
endmodule
