// Logisim project LengthModuleControlUnit.circ as structural Verilog: 1 circuit, main circuit LengthModuleContolUnit
module LengthModuleContolUnit (
  input  [3:0] len,
  input  eq,
  input  go,
  input  CLK,
  input  CLR,
  output [3:0] length,
  output finish,
  output loadStr,
  output selectL,
  output loadL
);

  wire and_8_out, and_9_out, and_10_out, not_1_out, not_2_out, not_3_out;
  wire [0:0] or_1_out;
  wire [1:1] register_1_q;

  not not_1 (not_1_out, eq);
  not not_2 (not_2_out, register_1_q[1]);
  not not_3 (not_3_out, loadL);
  and and_1 (length[0], len[0], finish);
  and and_2 (length[1], len[1], finish);
  and and_3 (length[2], len[2], finish);
  and and_4 (length[3], len[3], finish);
  and and_5 (finish, not_3_out, register_1_q[1]);
  and and_6 (loadStr, loadL, not_2_out);
  and and_7 (selectL, loadL, register_1_q[1]);
  and and_8 (and_8_out, not_1_out, loadL);
  or or_1 (or_1_out[0], and_8_out, and_9_out, and_10_out);
  and and_9 (and_9_out, loadL, not_2_out);
  and and_10 (and_10_out, go, not_2_out);
  Register #(.width(2)) register_1 (
    .D({loadL, or_1_out[0]}), .en(1'b1), .Q({register_1_q[1], loadL}), .clk(CLK), .clr(CLR));
endmodule
