// Logisim project LengthModuleDatapath.circ as structural Verilog: 1 circuit, main circuit LengthModuleDatapath
module LengthModuleDatapath (
  input  selectL,
  input  loadL,
  input  CLK,
  input  CLR,
  input  loadStr,
  input  [31:0] str_in_Last32,
  input  [31:0] str_in_First32,
  output [3:0] len,
  output eq
);

  wire [3:0] adder_1_out, length_q, multiplexer_1_out;
  wire [7:0] multiplexer_2_out;
  wire [31:0] strFirst32_q, strLast32_q;

  Register #(.width(4)) length (.D(multiplexer_1_out), .en(loadL), .Q(length_q), .clk(CLK), .clr(CLR));
  Multiplexer #(.width(4), .enable("false")) multiplexer_1 (
    .in0(4'b0000), .in1(adder_1_out), .out(multiplexer_1_out), .sel(selectL));
  Register #(.width(32)) strLast32 (.D(str_in_Last32), .en(loadStr), .Q(strLast32_q), .clk(CLK), .clr(CLR));
  Register #(.width(32)) strFirst32 (.D(str_in_First32), .en(loadStr), .Q(strFirst32_q), .clk(CLK), .clr(CLR));
  Adder #(.width(4)) adder_1 (.a(length_q), .b(4'b0001), .out(adder_1_out), .cin(1'b0));  // open: cout
  Subtractor #(.width(4)) subtractor_1 (.a(length_q), .b(4'b0001), .out(len), .bin(1'b0));  // open: bout
  Multiplexer #(.select(4), .width(8), .enable("false")) multiplexer_2 (
    .in0(strLast32_q[7:0]), .in1(strLast32_q[15:8]), .in2(strLast32_q[23:16]), .in3(strLast32_q[31:24]),
    .in4(strFirst32_q[7:0]), .in5(strFirst32_q[15:8]), .in6(strFirst32_q[23:16]), .in7(strFirst32_q[31:24]),
    .in8({8{1'b0}}), .out(multiplexer_2_out), .sel(length_q));  // open: in9, in10, in11, in12, in13, in14, in15
  Comparator #(.mode("unsigned")) comparator_1 (.a(multiplexer_2_out), .b({8{1'b0}}), .eq(eq));  // open: gt, lt
endmodule
