// Logisim project Printer.circ as structural Verilog: 1 circuit, main circuit Printer
module Printer (
  input  [31:0] first32bit,
  input  [31:0] last32bit,
  input  [3:0] length,
  input  go,
  input  CLK,
  input  CLR,
  output [6:0] out,
  output out_clr,
  output out_en,
  output finish
);

  wire printercontrolunit_1_li, printercontrolunit_1_si, printerdatapath_1_gt;

  PrinterControlUnit printercontrolunit_1 (
    .go(go), .gt(printerdatapath_1_gt), .CLK(CLK), .finish(finish), .out_en(out_en), .out_clr(out_clr),
    .si(printercontrolunit_1_si), .li(printercontrolunit_1_li), .CLR(CLR));
  PrinterDatapath printerdatapath_1 (
    .last32bit(last32bit), .first32bit(first32bit), .si(printercontrolunit_1_si),
    .li(printercontrolunit_1_li), .length(length), .CLK(CLK), .gt(printerdatapath_1_gt), .out(out), .CLR(CLR));
endmodule
