// Logisim project PrinterControlUnit.circ as structural Verilog: 1 circuit, main circuit PrinterControlUnit
module PrinterControlUnit (
  input  go,
  input  gt,
  input  CLK,
  input  CLR,
  output finish,
  output out_clr,
  output out_en,
  output si,
  output li
);

  wire and_4_out, and_5_out, and_6_out, not_1_out, not_2_out, not_3_out;
  wire [1:0] or_1_out;
  wire [1:1] register_1_q;

  not not_1 (not_1_out, register_1_q[1]);
  not not_2 (not_2_out, li);
  not not_3 (not_3_out, gt);
  and and_1 (finish, not_3_out, not_2_out, register_1_q[1]);
  and and_2 (out_clr, li, not_1_out);
  and and_3 (out_en, li, register_1_q[1]);
  and and_4 (and_4_out, gt, not_2_out, register_1_q[1]);
  or or_1 (or_1_out[0], and_4_out, and_5_out);
  and and_5 (and_5_out, go, not_2_out, not_1_out);
  or or_2 (or_1_out[1], li, and_6_out);
  and and_6 (and_6_out, gt, register_1_q[1]);
  Register #(.width(2)) register_1 (.D(or_1_out), .en(1'b1), .Q({register_1_q[1], li}), .clk(CLK), .clr(CLR));

  assign si = out_en;
endmodule
