// Logisim project PrinterDatapath.circ as structural Verilog: 1 circuit, main circuit PrinterDatapath
module PrinterDatapath (
  input  [31:0] last32bit,
  input  [31:0] first32bit,
  input  [3:0] length,
  input  si,
  input  li,
  input  CLK,
  input  CLR,
  output [6:0] out,
  output gt
);

  wire [2:0] bit_extender_1_out;
  wire [3:0] i_q, multiplexer_1_out, subtractor_1_out;
  wire [7:0] multiplexer_2_out;

  Register #(.width(4)) i (.D(multiplexer_1_out), .en(li), .Q(i_q), .clk(CLK), .clr(CLR));
  Multiplexer #(.width(4), .enable("false")) multiplexer_1 (
    .in0(length), .in1(subtractor_1_out), .out(multiplexer_1_out), .sel(si));
  Multiplexer #(.select(3), .width(8), .enable("false")) multiplexer_2 (
    .in0(last32bit[7:0]), .in1(last32bit[15:8]), .in2(last32bit[23:16]), .in3(last32bit[31:24]),
    .in4(first32bit[7:0]), .in5(first32bit[15:8]), .in6(first32bit[23:16]), .in7(first32bit[31:24]),
    .out(multiplexer_2_out), .sel(bit_extender_1_out));
  Bit_Extender #(.in_width(4), .out_width(3)) bit_extender_1 (.in(subtractor_1_out), .out(bit_extender_1_out));
  Subtractor #(.width(4)) subtractor_1 (.a(i_q), .b(4'b0001), .out(subtractor_1_out), .bin(1'b0));  // open: bout
  Comparator #(.width(4), .mode("unsigned")) comparator_1 (.a(i_q), .b(4'b0000), .gt(gt));  // open: eq, lt
  Bit_Extender #(.out_width(7)) bit_extender_2 (.in(multiplexer_2_out), .out(out));
endmodule
