// Logisim project ScoreModule.circ as structural Verilog: 1 circuit, main circuit ScoreModule
module ScoreModule (
  input  in,
  output point,
  output [3:0] score
);

  wire d_ff_1_qn, d_ff_2_qn, d_ff_3_qn, d_ff_4_qn;

  D_Flip_Flop d_ff_1 (.clk(in), .D(d_ff_1_qn), .Q(score[0]), .Qn(d_ff_1_qn), .preset(1'b0), .en(1'b1), .reset(1'b0));
  D_Flip_Flop d_ff_2 (
    .clk(d_ff_1_qn), .D(d_ff_2_qn), .Q(score[1]), .Qn(d_ff_2_qn), .preset(1'b0), .en(1'b1), .reset(1'b0));
  D_Flip_Flop d_ff_3 (
    .clk(d_ff_2_qn), .D(d_ff_3_qn), .Q(score[2]), .Qn(d_ff_3_qn), .preset(1'b0), .en(1'b1), .reset(1'b0));
  D_Flip_Flop d_ff_4 (
    .clk(d_ff_3_qn), .D(d_ff_4_qn), .Q(score[3]), .Qn(d_ff_4_qn), .preset(1'b0), .en(1'b1), .reset(1'b0));

  assign point = 1'b0;
endmodule
