// Logisim project main.circ as structural Verilog: 1 circuit, main circuit main
module main (
  input  [31:0] first32bit,
  input  [31:0] last32bit
);

  wire a_out, b_out, c_out, clock_1_out, d_out, e_out, f_out, g_out, go_out, goRand_out, h_out,
       hangman_1_losepoint, hangman_1_out_clr, hangman_1_out_en, hangman_1_s0, hangman_1_s1, hangman_1_s2,
       hangman_1_s3, hangman_1_s4, hangman_1_s5, hangman_1_s6, hangman_1_s7, hangman_1_winpoint, i_out,
       j_out, k_out, l_out, m_out, n_out, o_out, p_out, q_out, r_out, restart_out, s_out, t_out, u_out,
       v_out, w_out, x_out, y_out, z_out;
  wire [3:0] hangman_1_lose, hangman_1_win;
  wire [6:0] hangman_1_out;
  wire [15:0] hangman_1_c1, hangman_1_c2, hangman_1_c3, hangman_1_c4, hangman_1_c5, hangman_1_c6,
       hangman_1_c7, hangman_1_c8;

  Button a (.out(a_out));
  Button b (.out(b_out));
  Button c (.out(c_out));
  Button d (.out(d_out));
  Button e (.out(e_out));
  Button f (.out(f_out));
  Button g (.out(g_out));
  Button h (.out(h_out));
  Button i (.out(i_out));
  Button j (.out(j_out));
  Button k (.out(k_out));
  Button l (.out(l_out));
  Button m (.out(m_out));
  Button n (.out(n_out));
  Button o (.out(o_out));
  Button p (.out(p_out));
  Button q (.out(q_out));
  Button r (.out(r_out));
  Button s (.out(s_out));
  Button t (.out(t_out));
  Button u (.out(u_out));
  Button v (.out(v_out));
  Button w (.out(w_out));
  Button x (.out(x_out));
  Button y (.out(y_out));
  Button z (.out(z_out));
  Button restart (.out(restart_out));
  Button go (.out(go_out));
  Hangman hangman_1 (
    .a(a_out), .b(b_out), .c(c_out), .strfirst32(first32bit), .d(d_out), .e(e_out), .f(f_out), .g(g_out),
    .h(h_out), .i(i_out), .j(j_out), .k(k_out), .l(l_out), .m(m_out), .n(n_out), .o(o_out), .p(p_out),
    .q(q_out), .r(r_out), .s(s_out), .t(t_out), .u(u_out), .v(v_out), .w(w_out), .x(x_out), .y(y_out),
    .z(z_out), .restart(restart_out), .go(go_out), .goRand(goRand_out), .CLK(clock_1_out),
    .strlast32(last32bit), .s0(hangman_1_s0), .s1(hangman_1_s1), .out_clr(hangman_1_out_clr),
    .s2(hangman_1_s2), .out_en(hangman_1_out_en), .s3(hangman_1_s3), .out(hangman_1_out), .s4(hangman_1_s4),
    .s5(hangman_1_s5), .s6(hangman_1_s6), .s7(hangman_1_s7), .win(hangman_1_win),
    .winPoint(hangman_1_winpoint), .lose(hangman_1_lose), .losePoint(hangman_1_losepoint), .c1(hangman_1_c1),
    .c2(hangman_1_c2), .c3(hangman_1_c3), .c4(hangman_1_c4), .c5(hangman_1_c5), .c6(hangman_1_c6),
    .c7(hangman_1_c7), .c8(hangman_1_c8));
  Button goRand (.out(goRand_out));
  _7_Segment_Display u_7_segment_display_1 (
    .g(hangman_1_s3), .f(hangman_1_s1), .a(hangman_1_s0), .b(hangman_1_s2), .e(hangman_1_s4),
    .d(hangman_1_s6), .c(hangman_1_s5), .dp(hangman_1_s7));
  Clock clock_1 (.out(clock_1_out));
  Hex_Digit_Display hex_digit_display_1 (.value(hangman_1_win), .dp(hangman_1_winpoint));
  TTY tty_1 (.data(hangman_1_out), .clk(clock_1_out), .we(hangman_1_out_en), .clr(hangman_1_out_clr));
  Hex_Digit_Display hex_digit_display_2 (.value(hangman_1_lose), .dp(hangman_1_losepoint));
  DotMatrix #(.matrixcols(8), .matrixrows(16)) dotmatrix_1 (
    .col0(hangman_1_c1), .col1(hangman_1_c2), .col2(hangman_1_c3), .col3(hangman_1_c4), .col4(hangman_1_c5),
    .col5(hangman_1_c6), .col6(hangman_1_c7), .col7(hangman_1_c8));

  // Notes on the sheet:
  //   length
  //   User
  //   Display
  //   Computer
endmodule
