// Logisim project Project.circ as structural Verilog: 1 circuit, main circuit main
module main (
);

  wire and_1_out, and_3_out, and_4_out, and_5_out, and_7_out, and_8_out, and_9_out, and_10_out, and_11_out,
       and_12_out, and_13_out, and_14_out, and_15_out, and_17_out, and_18_out, and_19_out, and_20_out,
       and_21_out, and_22_out, and_23_out, and_24_out, and_25_out, and_26_out, and_27_out, and_28_out,
       and_29_out, and_30_out, and_31_out, and_32_out, and_33_out, and_34_out, and_35_out, and_36_out,
       and_37_out, and_38_out, and_39_out, and_40_out, and_41_out, and_42_out, and_43_out, and_44_out,
       and_45_out, and_46_out, and_47_out, and_48_out, and_49_out, and_50_out, and_51_out, and_53_out,
       and_54_out, and_55_out, and_56_out, and_57_out, and_58_out, and_59_out, and_60_out, and_61_out,
       and_62_out, and_63_out, and_64_out, and_65_out, and_66_out, and_67_out, and_68_out, bi_2_out, bi_out,
       clock_1_out, not_1_out, not_2_out, not_3_out, not_4_out, not_5_out, not_6_out, not_7_out, not_8_out,
       not_9_out, not_10_out, not_11_out, not_12_out, not_13_out, not_14_out, not_15_out, not_16_out,
       not_17_out, not_18_out, not_19_out, not_20_out, not_21_out, not_22_out, not_23_out, not_24_out,
       not_25_out, not_26_out, not_27_out, not_28_out, not_29_out, not_30_out, not_31_out, not_32_out,
       not_33_out, not_34_out, not_35_out, not_36_out, not_37_out, not_38_out, not_39_out, not_40_out,
       not_41_out, not_42_out, not_43_out, not_44_out, not_45_out, not_46_out, not_47_out, not_48_out,
       not_49_out, not_50_out, not_51_out, not_52_out, not_53_out, not_54_out, not_55_out, not_56_out,
       not_57_out, not_58_out, not_59_out, not_60_out, not_61_out, not_62_out, not_63_out, not_64_out,
       not_65_out, not_66_out, not_67_out, not_68_out, not_69_out, not_70_out, not_71_out, not_72_out,
       not_73_out, not_74_out, not_75_out, not_76_out, not_77_out, not_78_out, not_79_out, not_80_out,
       not_81_out, not_82_out, not_83_out, not_84_out, not_85_out, not_86_out, not_87_out, not_88_out,
       not_89_out, not_90_out, not_91_out, not_92_out, not_93_out, not_94_out, not_95_out, not_96_out,
       not_97_out, not_98_out, not_99_out, not_100_out, not_101_out, not_102_out, not_103_out, not_104_out,
       not_105_out, not_106_out, not_107_out, not_108_out, not_109_out, not_110_out, not_111_out,
       not_112_out, not_113_out, not_114_out, not_115_out, not_116_out, not_117_out, not_118_out,
       not_119_out, not_120_out, not_121_out, not_122_out, not_123_out, not_124_out, not_125_out,
       not_126_out, not_127_out, not_128_out, not_129_out, not_130_out, not_131_out, not_132_out,
       not_133_out, not_134_out, not_135_out, r2_out, r_out;
  wire [1:0] and_2_out, and_6_out, and_16_out, and_52_out, register_1_q, register_2_q, register_4_q,
       register_6_q;
  wire [2:0] or_8_out, register_3_q;
  wire [3:0] or_10_out, or_15_out, register_5_q, register_7_q;

  Clock clock_1 (.out(clock_1_out));
  Button bi (.out(bi_out));
  Button r (.out(r_out));
  Button bi_2 (.out(bi_2_out));
  and and_1 (and_1_out, register_1_q[0], not_1_out);
  not not_1 (not_1_out, register_1_q[1]);
  not not_2 (not_2_out, register_1_q[0]);
  and and_2 (and_2_out[0], bi_out, not_2_out, not_3_out);
  not not_3 (not_3_out, register_1_q[1]);
  not not_4 (not_4_out, register_1_q[0]);
  and and_3 (and_3_out, bi_out, not_4_out, register_1_q[1]);
  and and_4 (and_4_out, bi_out, register_1_q[0], not_5_out);
  not not_5 (not_5_out, register_1_q[1]);
  Register #(.width(2)) register_1 (.D(and_2_out), .Q(register_1_q), .clk(clock_1_out));  // open: en, clr
  and and_5 (and_5_out, register_2_q[0], not_6_out);
  not not_6 (not_6_out, register_2_q[1]);
  not not_7 (not_7_out, register_2_q[0]);
  and and_6 (and_6_out[0], bi_2_out, not_7_out, not_8_out);
  not not_8 (not_8_out, register_2_q[1]);
  and and_7 (and_7_out, bi_2_out, not_9_out, register_2_q[1]);
  not not_9 (not_9_out, register_2_q[0]);
  and and_8 (and_8_out, bi_2_out, register_2_q[0], not_10_out);
  not not_10 (not_10_out, register_2_q[1]);
  Register #(.width(2)) register_2 (.D(and_6_out), .Q(register_2_q), .clk(clock_1_out));  // open: en, clr
  or or_1 (and_2_out[1], and_3_out, and_4_out);
  or or_2 (and_6_out[1], and_7_out, and_8_out);
  Register #(.width(3)) register_3 (.D(or_8_out), .Q(register_3_q), .clk(clock_1_out));  // open: en, clr
  Register #(.width(2)) register_4 (.D(and_16_out), .Q(register_4_q), .clk(clock_1_out));  // open: en, clr
  and and_9 (and_9_out, register_3_q[2], register_3_q[1], not_11_out);
  not not_11 (not_11_out, register_3_q[0]);
  not not_12 (not_12_out, r_out);
  not not_13 (not_13_out, and_5_out);
  and and_10 (and_10_out, not_12_out, not_13_out, and_1_out, not_14_out, not_15_out);
  not not_14 (not_14_out, register_3_q[0]);
  not not_15 (not_15_out, register_3_q[1]);
  not not_16 (not_16_out, r_out);
  not not_17 (not_17_out, and_5_out);
  and and_11 (and_11_out, not_16_out, not_17_out, not_18_out, register_3_q[2]);
  not not_18 (not_18_out, register_3_q[1]);
  not not_19 (not_19_out, r_out);
  and and_12 (and_12_out, not_19_out, register_3_q[0], not_20_out, register_3_q[2]);
  not not_20 (not_20_out, register_3_q[1]);
  not not_21 (not_21_out, r_out);
  and and_13 (and_13_out, not_21_out, and_1_out, not_22_out, register_3_q[2]);
  not not_22 (not_22_out, register_3_q[0]);
  not not_23 (not_23_out, r_out);
  not not_24 (not_24_out, register_3_q[0]);
  and and_14 (and_14_out, not_23_out, not_24_out, register_3_q[1], register_3_q[2]);
  and and_15 (and_15_out, register_4_q[0], not_25_out);
  not not_25 (not_25_out, register_4_q[1]);
  and and_16 (and_16_out[0], and_9_out, not_26_out, not_27_out);
  not not_26 (not_26_out, register_4_q[0]);
  not not_27 (not_27_out, register_4_q[1]);
  and and_17 (and_17_out, and_9_out, not_28_out, register_4_q[1]);
  not not_28 (not_28_out, register_4_q[0]);
  and and_18 (and_18_out, and_9_out, register_4_q[0], not_29_out);
  not not_29 (not_29_out, register_4_q[1]);
  not not_30 (not_30_out, register_3_q[1]);
  or or_3 (or_8_out[2], and_10_out, and_11_out, and_12_out, and_13_out, and_14_out);
  or or_4 (and_16_out[1], and_17_out, and_18_out);
  and and_19 (and_19_out, register_3_q[2], not_30_out, register_3_q[0]);
  not not_31 (not_31_out, r2_out);
  not not_32 (not_32_out, register_5_q[1]);
  not not_33 (not_33_out, r2_out);
  not not_34 (not_34_out, register_5_q[2]);
  not not_35 (not_35_out, r2_out);
  not not_36 (not_36_out, and_15_out);
  not not_37 (not_37_out, r2_out);
  not not_38 (not_38_out, register_5_q[0]);
  not not_39 (not_39_out, r2_out);
  not not_40 (not_40_out, register_5_q[3]);
  Register #(.width(4)) register_5 (.D(or_10_out), .Q(register_5_q), .clk(clock_1_out));  // open: en, clr
  Hex_Digit_Display hex_digit_display_1 (.value(register_5_q));  // open: dp
  and and_20 (and_20_out, register_3_q[2], not_41_out, not_42_out);
  not not_41 (not_41_out, register_3_q[1]);
  not not_42 (not_42_out, register_3_q[0]);
  not not_43 (not_43_out, r_out);
  not not_44 (not_44_out, and_5_out);
  and and_21 (and_21_out, not_43_out, not_44_out, and_1_out, register_3_q[0], not_45_out, register_3_q[2]);
  not not_45 (not_45_out, register_3_q[1]);
  not not_46 (not_46_out, r_out);
  not not_47 (not_47_out, and_1_out);
  and and_22 (and_22_out, not_46_out, not_47_out, not_48_out, register_3_q[1]);
  not not_48 (not_48_out, register_3_q[0]);
  not not_49 (not_49_out, r_out);
  not not_50 (not_50_out, register_3_q[0]);
  and and_23 (and_23_out, not_49_out, not_50_out, register_3_q[1], register_3_q[2]);
  not not_51 (not_51_out, r_out);
  and and_24 (and_24_out, not_51_out, and_5_out, register_3_q[1], not_52_out);
  not not_52 (not_52_out, register_3_q[2]);
  not not_53 (not_53_out, r_out);
  and and_25 (and_25_out, not_53_out, register_3_q[0], register_3_q[1], not_54_out);
  not not_54 (not_54_out, register_3_q[2]);
  not not_55 (not_55_out, r_out);
  and and_26 (and_26_out, not_55_out, and_5_out, not_56_out, register_3_q[0], not_57_out);
  not not_56 (not_56_out, and_1_out);
  not not_57 (not_57_out, register_3_q[2]);
  and and_27 (and_27_out, not_31_out, not_32_out, register_5_q[3]);
  and and_28 (and_28_out, not_33_out, not_34_out, register_5_q[3]);
  and and_29 (and_29_out, not_35_out, not_36_out, register_5_q[3]);
  and and_30 (and_30_out, not_37_out, not_38_out, register_5_q[3]);
  and and_31 (and_31_out, not_39_out, and_15_out, register_5_q[0], register_5_q[1], register_5_q[2], not_40_out);
  LED led_1 (.in(and_9_out));
  LED led_2 (.in(and_19_out));
  not not_58 (not_58_out, register_3_q[2]);
  not not_59 (not_59_out, register_3_q[1]);
  not not_60 (not_60_out, register_3_q[0]);
  or or_5 (or_8_out[1], and_21_out, and_22_out, and_23_out, and_24_out, and_25_out, and_26_out);
  or or_6 (or_10_out[3], and_27_out, and_28_out, and_29_out, and_30_out, and_31_out);
  Button r2 (.out(r2_out));
  LED led_3 (.in(and_32_out));
  LED led_4 (.in(and_33_out));
  LED led_5 (.in(and_20_out));
  and and_32 (and_32_out, not_58_out, not_59_out, not_60_out);
  not not_61 (not_61_out, r_out);
  not not_62 (not_62_out, and_5_out);
  not not_63 (not_63_out, register_3_q[0]);
  not not_64 (not_64_out, register_3_q[1]);
  not not_65 (not_65_out, r_out);
  not not_66 (not_66_out, register_3_q[2]);
  not not_67 (not_67_out, r_out);
  not not_68 (not_68_out, and_5_out);
  not not_69 (not_69_out, register_3_q[2]);
  not not_70 (not_70_out, r_out);
  not not_71 (not_71_out, register_3_q[1]);
  not not_72 (not_72_out, r_out);
  not not_73 (not_73_out, and_5_out);
  not not_74 (not_74_out, and_1_out);
  not not_75 (not_75_out, register_3_q[1]);
  not not_76 (not_76_out, r_out);
  not not_77 (not_77_out, and_1_out);
  not not_78 (not_78_out, register_3_q[0]);
  not not_79 (not_79_out, register_3_q[2]);
  not not_80 (not_80_out, r2_out);
  not not_81 (not_81_out, and_15_out);
  not not_82 (not_82_out, r2_out);
  not not_83 (not_83_out, register_5_q[1]);
  not not_84 (not_84_out, r2_out);
  not not_85 (not_85_out, register_5_q[0]);
  not not_86 (not_86_out, r2_out);
  not not_87 (not_87_out, register_5_q[2]);
  LED led_6 (.in(and_44_out));
  LED led_7 (.in(and_48_out));
  not not_88 (not_88_out, register_3_q[2]);
  and and_33 (and_33_out, not_88_out, not_89_out, register_3_q[0]);
  not not_89 (not_89_out, register_3_q[1]);
  and and_34 (and_34_out, not_61_out, not_62_out, and_1_out, not_63_out, not_64_out, register_3_q[2]);
  and and_35 (and_35_out, not_65_out, register_3_q[0], register_3_q[1], not_66_out);
  and and_36 (and_36_out, not_67_out, not_68_out, and_1_out, register_3_q[1], not_69_out);
  and and_37 (and_37_out, not_70_out, and_5_out, and_1_out, register_3_q[0], not_71_out);
  and and_38 (and_38_out, not_72_out, not_73_out, not_74_out, register_3_q[0], not_75_out);
  and and_39 (and_39_out, not_76_out, and_5_out, not_77_out, not_78_out, not_79_out);
  and and_40 (and_40_out, not_80_out, not_81_out, register_5_q[2]);
  and and_41 (and_41_out, not_82_out, not_83_out, register_5_q[2]);
  or or_7 (or_10_out[2], and_40_out, and_41_out, and_42_out, and_43_out);
  and and_42 (and_42_out, not_84_out, not_85_out, register_5_q[2]);
  and and_43 (and_43_out, not_86_out, and_15_out, register_5_q[0], register_5_q[1], not_87_out);
  Hex_Digit_Display hex_digit_display_2 (.value(register_7_q));  // open: dp
  not not_90 (not_90_out, register_3_q[2]);
  not not_91 (not_91_out, register_3_q[0]);
  or or_8 (or_8_out[0], and_34_out, and_35_out, and_36_out, and_37_out, and_38_out, and_39_out);
  not not_92 (not_92_out, r2_out);
  not not_93 (not_93_out, and_15_out);
  not not_94 (not_94_out, r2_out);
  not not_95 (not_95_out, register_5_q[0]);
  not not_96 (not_96_out, r2_out);
  not not_97 (not_97_out, register_5_q[1]);
  and and_44 (and_44_out, not_90_out, register_3_q[1], not_91_out);
  and and_45 (and_45_out, not_92_out, not_93_out, register_5_q[1]);
  and and_46 (and_46_out, not_94_out, not_95_out, register_5_q[1]);
  and and_47 (and_47_out, not_96_out, and_15_out, register_5_q[0], not_97_out);
  not not_98 (not_98_out, register_3_q[2]);
  and and_48 (and_48_out, not_98_out, register_3_q[1], register_3_q[0]);
  or or_9 (or_10_out[1], and_45_out, and_46_out, and_47_out);
  not not_99 (not_99_out, r2_out);
  not not_100 (not_100_out, and_15_out);
  and and_49 (and_49_out, not_99_out, not_100_out, register_5_q[0]);
  not not_101 (not_101_out, r2_out);
  and and_50 (and_50_out, not_101_out, and_15_out, not_102_out);
  not not_102 (not_102_out, register_5_q[0]);
  or or_10 (or_10_out[0], and_49_out, and_50_out);
  not not_103 (not_103_out, register_6_q[1]);
  not not_104 (not_104_out, register_6_q[0]);
  not not_105 (not_105_out, register_6_q[1]);
  not not_106 (not_106_out, register_6_q[0]);
  not not_107 (not_107_out, register_6_q[1]);
  Register #(.width(2)) register_6 (.D(and_52_out), .Q(register_6_q), .clk(clock_1_out));  // open: en, clr
  and and_51 (and_51_out, register_6_q[0], not_103_out);
  and and_52 (and_52_out[0], and_48_out, not_104_out, not_105_out);
  and and_53 (and_53_out, and_48_out, not_106_out, register_6_q[1]);
  and and_54 (and_54_out, and_48_out, register_6_q[0], not_107_out);
  or or_11 (and_52_out[1], and_53_out, and_54_out);
  not not_108 (not_108_out, r2_out);
  not not_109 (not_109_out, register_7_q[1]);
  not not_110 (not_110_out, r2_out);
  not not_111 (not_111_out, register_7_q[2]);
  not not_112 (not_112_out, r2_out);
  not not_113 (not_113_out, and_51_out);
  not not_114 (not_114_out, r2_out);
  not not_115 (not_115_out, register_7_q[0]);
  not not_116 (not_116_out, r2_out);
  not not_117 (not_117_out, register_7_q[3]);
  Register #(.width(4)) register_7 (.D(or_15_out), .Q(register_7_q), .clk(clock_1_out));  // open: en, clr
  and and_55 (and_55_out, not_108_out, not_109_out, register_7_q[3]);
  and and_56 (and_56_out, not_110_out, not_111_out, register_7_q[3]);
  and and_57 (and_57_out, not_112_out, not_113_out, register_7_q[3]);
  and and_58 (and_58_out, not_114_out, not_115_out, register_7_q[3]);
  and and_59 (and_59_out, not_116_out, and_51_out, register_7_q[0], register_7_q[1], register_7_q[2], not_117_out);
  or or_12 (or_15_out[3], and_55_out, and_56_out, and_57_out, and_58_out, and_59_out);
  not not_118 (not_118_out, r2_out);
  and and_60 (and_60_out, not_118_out, not_119_out, register_7_q[2]);
  not not_119 (not_119_out, and_51_out);
  not not_120 (not_120_out, r2_out);
  and and_61 (and_61_out, not_120_out, not_121_out, register_7_q[2]);
  not not_121 (not_121_out, register_7_q[1]);
  not not_122 (not_122_out, r2_out);
  and and_62 (and_62_out, not_122_out, not_123_out, register_7_q[2]);
  not not_123 (not_123_out, register_7_q[0]);
  not not_124 (not_124_out, r2_out);
  and and_63 (and_63_out, not_124_out, and_51_out, register_7_q[0], register_7_q[1], not_125_out);
  not not_125 (not_125_out, register_7_q[2]);
  or or_13 (or_15_out[2], and_60_out, and_61_out, and_62_out, and_63_out);
  not not_126 (not_126_out, r2_out);
  not not_127 (not_127_out, and_51_out);
  not not_128 (not_128_out, r2_out);
  not not_129 (not_129_out, register_7_q[0]);
  not not_130 (not_130_out, r2_out);
  not not_131 (not_131_out, register_7_q[1]);
  and and_64 (and_64_out, not_126_out, not_127_out, register_7_q[1]);
  and and_65 (and_65_out, not_128_out, not_129_out, register_7_q[1]);
  or or_14 (or_15_out[1], and_64_out, and_65_out, and_66_out);
  and and_66 (and_66_out, not_130_out, and_51_out, register_7_q[0], not_131_out);
  not not_132 (not_132_out, r2_out);
  not not_133 (not_133_out, and_51_out);
  not not_134 (not_134_out, r2_out);
  not not_135 (not_135_out, register_7_q[0]);
  and and_67 (and_67_out, not_132_out, not_133_out, register_7_q[0]);
  and and_68 (and_68_out, not_134_out, and_51_out, not_135_out);
  or or_15 (or_15_out[0], and_67_out, and_68_out);

  // Notes on the sheet:
  //   b1
  //   b2
endmodule
