// Logisim project ControlUnit.circ as structural Verilog: 1 circuit, main circuit Control Unit
module Control_Unit (
  input  go,
  input  et,
  input  lt,
  input  o,
  input  CLK,
  input  CLR,
  output la,
  output sa,
  output lb,
  output sb,
  output lmult,
  output clr_mult,
  output [1:0] op,
  output as,
  output oflw
);

  wire and_1_out, and_2_out, and_3_out, and_4_out, and_5_out, and_6_out, and_7_out, and_8_out, and_9_out,
       and_10_out, and_11_out, and_12_out, and_13_out, and_14_out, and_15_out, and_16_out, not_1_out,
       not_2_out, not_3_out, not_4_out, not_5_out, not_6_out, not_7_out, not_8_out, not_9_out, not_10_out,
       or_5_out, xor_1_out, xor_2_out;
  wire [3:0] or_1_out, register_1_q;

  not not_1 (not_1_out, register_1_q[0]);
  not not_2 (not_2_out, register_1_q[2]);
  not not_3 (not_3_out, register_1_q[3]);
  not not_4 (not_4_out, register_1_q[1]);
  and and_1 (and_1_out, go, not_1_out, not_4_out, not_3_out);
  not not_5 (not_5_out, o);
  and and_2 (and_2_out, not_5_out, not_1_out, register_1_q[1], not_3_out);
  and and_3 (and_3_out, not_1_out, register_1_q[1], not_2_out, not_3_out);
  and and_4 (and_4_out, not_1_out, not_4_out, register_1_q[2], not_3_out);
  and and_5 (and_5_out, register_1_q[0], register_1_q[1], register_1_q[2], not_3_out);
  not not_6 (not_6_out, et);
  and and_6 (and_6_out, not_6_out, register_1_q[0], not_4_out, not_3_out);
  and and_7 (and_7_out, register_1_q[0], not_4_out, not_2_out, not_3_out);
  and and_8 (and_8_out, lt, not_1_out, register_1_q[1], not_2_out, not_3_out);
  not not_7 (not_7_out, o);
  and and_9 (and_9_out, not_7_out, not_1_out, register_1_q[1], register_1_q[2], not_3_out);
  and and_10 (and_10_out, register_1_q[0], register_1_q[1], not_3_out);
  not not_8 (not_8_out, lt);
  and and_11 (and_11_out, not_8_out, register_1_q[1], not_2_out, not_3_out);
  not not_9 (not_9_out, et);
  and and_12 (and_12_out, not_9_out, not_4_out, register_1_q[2], not_3_out);
  and and_13 (and_13_out, not_1_out, not_4_out, register_1_q[2], not_3_out);
  not not_10 (not_10_out, o);
  and and_14 (and_14_out, not_10_out, register_1_q[1], register_1_q[2], not_3_out);
  and and_15 (and_15_out, o, not_1_out, register_1_q[1], register_1_q[2], not_3_out);
  and and_16 (and_16_out, not_1_out, not_4_out, not_2_out, register_1_q[3]);
  Register #(.width(4)) register_1 (.D(or_1_out), .en(1'b1), .Q(register_1_q), .clk(CLK), .clr(CLR));
  or or_1 (or_1_out[0], and_1_out, and_2_out, and_3_out, and_4_out, and_5_out);
  or or_2 (or_1_out[1], and_6_out, and_7_out, and_8_out, and_9_out);
  or or_3 (or_1_out[2], and_10_out, and_11_out, and_12_out, and_13_out, and_14_out);
  or or_4 (or_1_out[3], and_15_out, and_16_out);
  or or_5 (or_5_out, not_2_out, register_1_q[1]);
  xor xor_1 (xor_1_out, register_1_q[2], register_1_q[0]);
  xor xor_2 (xor_2_out, register_1_q[2], register_1_q[0]);
  and and_17 (la, or_5_out, not_3_out, register_1_q[0]);
  and and_18 (sa, not_3_out, register_1_q[1], register_1_q[0]);
  and and_19 (lb, xor_1_out, not_3_out, not_4_out);
  and and_20 (sb, not_3_out, register_1_q[2], not_4_out, not_1_out);
  and and_21 (lmult, not_3_out, register_1_q[2], register_1_q[1], not_1_out);
  and and_22 (clr_mult, not_3_out, not_2_out, not_4_out, register_1_q[0]);
  and and_23 (op[0], xor_2_out, not_3_out, register_1_q[1]);
  and and_24 (op[1], not_3_out, register_1_q[2], not_1_out);
  and and_25 (as, not_3_out, register_1_q[2], register_1_q[1], register_1_q[0]);
  and and_26 (oflw, register_1_q[3], not_2_out, not_4_out, not_1_out);
endmodule
