// Logisim project Datapath.circ as structural Verilog: 1 circuit, main circuit Datapath
module Datapath (
  input  [15:0] a,
  input  [15:0] b,
  input  la,
  input  sa,
  input  lb,
  input  sb,
  input  lmult,
  input  as,
  input  clr_mult,
  input  [1:0] op,
  input  CLK,
  output et,
  output lt,
  output OFLW,
  output [15:0] mult
);

  wire and_1_out, and_2_out, not_4_out, not_5_out, not_6_out;
  wire [15:0] a_q, adder_1_out, b_q, multiplexer_1_out, multiplexer_2_out, multiplexer_3_out,
       multiplexer_4_out, multiplexer_5_out, not_1_out, not_2_out, not_3_out;

  assign not_1_out = ~a;  // NOT_Gate not_1, 16 bits wide
  Multiplexer #(.width(16), .enable("false")) multiplexer_1 (
    .in0(a), .in1(adder_1_out), .out(multiplexer_1_out), .sel(sa));
  Register #(.width(16)) u_a (.D(multiplexer_1_out), .en(la), .Q(a_q), .clk(CLK), .clr(1'b0));
  Multiplexer #(.width(16), .enable("false")) multiplexer_2 (
    .in0(b), .in1(adder_1_out), .out(multiplexer_2_out), .sel(sb));
  Register #(.width(16)) u_b (.D(multiplexer_2_out), .en(lb), .Q(b_q), .clk(CLK), .clr(1'b0));
  Comparator #(.width(16)) comparator_1 (.a(a_q), .b({16{1'b0}}), .eq(et), .lt(lt));  // open: gt
  Register #(.width(16)) u_mult (.D(adder_1_out), .en(lmult), .Q(mult), .clk(CLK), .clr(clr_mult));
  assign not_2_out = ~b;  // NOT_Gate not_2, 16 bits wide
  Multiplexer #(.select(2), .width(16), .enable("false")) multiplexer_3 (
    .in0(a_q), .in1(not_1_out), .in2(not_2_out), .in3(mult), .out(multiplexer_3_out), .sel(op));
  Multiplexer #(.select(2), .width(16), .enable("false")) multiplexer_4 (
    .in0(16'h1), .in1(16'h1), .in2(16'h1), .in3(b_q), .out(multiplexer_4_out), .sel(op));
  Multiplexer #(.width(16), .enable("false")) multiplexer_5 (
    .in0(multiplexer_4_out), .in1(not_3_out), .out(multiplexer_5_out), .sel(as));
  assign not_3_out = ~multiplexer_4_out;  // NOT_Gate not_3, 16 bits wide
  Adder #(.width(16)) adder_1 (
    .a(multiplexer_5_out), .b(multiplexer_3_out), .out(adder_1_out), .cin(as));  // open: cout
  not not_4 (not_4_out, adder_1_out[15]);
  and and_1 (and_1_out, not_4_out, multiplexer_3_out[15], multiplexer_5_out[15]);
  not not_5 (not_5_out, multiplexer_3_out[15]);
  and and_2 (and_2_out, adder_1_out[15], not_5_out, not_6_out);
  not not_6 (not_6_out, multiplexer_5_out[15]);
  xor xor_1 (OFLW, and_1_out, and_2_out);
endmodule
