// Logisim project Project2_main.circ as structural Verilog: 1 circuit, main circuit main
module main (
  input  [15:0] a,
  input  [15:0] b,
  output [15:0] mult
);

  wire button_syncronizer_1_out, clock_1_out, clr_out, control_unit_1_as, control_unit_1_clr_mult,
       control_unit_1_la, control_unit_1_lb, control_unit_1_lmult, control_unit_1_oflw, control_unit_1_sa,
       control_unit_1_sb, datapath_1_et, datapath_1_lt, datapath_1_oflw, go_out;
  wire [1:0] control_unit_1_op;

  Button go (.out(go_out));
  Button clr (.out(clr_out));
  Button_Syncronizer button_syncronizer_1 (.in(go_out), .CLK(clock_1_out), .out(button_syncronizer_1_out));
  Clock clock_1 (.out(clock_1_out));
  Control_Unit control_unit_1 (
    .go(button_syncronizer_1_out), .et(datapath_1_et), .lt(datapath_1_lt), .o(datapath_1_oflw),
    .CLK(clock_1_out), .CLR(clr_out), .la(control_unit_1_la), .sa(control_unit_1_sa), .lb(control_unit_1_lb),
    .sb(control_unit_1_sb), .lmult(control_unit_1_lmult), .clr_mult(control_unit_1_clr_mult),
    .op(control_unit_1_op), .as(control_unit_1_as), .oflw(control_unit_1_oflw));
  Datapath datapath_1 (
    .a(a), .b(b), .la(control_unit_1_la), .sa(control_unit_1_sa), .lb(control_unit_1_lb),
    .sb(control_unit_1_sb), .lmult(control_unit_1_lmult), .clr_mult(control_unit_1_clr_mult),
    .CLK(clock_1_out), .et(datapath_1_et), .lt(datapath_1_lt), .OFLW(datapath_1_oflw),
    .op(control_unit_1_op), .as(control_unit_1_as), .mult(mult));
  LED OVERFLOW (.in(control_unit_1_oflw));
endmodule
