// Logisim project lab3.circ as structural Verilog: 1 circuit, main circuit main
module main (
  input  b,
  input  a
);

  wire and_1_out, and_2_out, and_3_out, and_4_out, and_5_out, clock_1_out, not_1_out, not_2_out, not_3_out,
       not_4_out, not_5_out, not_6_out, or_1_out;
  wire [1:0] or_2_out, register_1_q;

  Clock clock_1 (.out(clock_1_out));
  not not_1 (not_1_out, a);
  or or_1 (or_1_out, not_1_out, register_1_q[0]);
  and and_1 (and_1_out, or_1_out, register_1_q[1], b);
  not not_2 (not_2_out, b);
  and and_2 (and_2_out, not_2_out, a, not_3_out);
  not not_3 (not_3_out, register_1_q[1]);
  and and_3 (and_3_out, b, register_1_q[1]);
  not not_4 (not_4_out, a);
  not not_5 (not_5_out, register_1_q[0]);
  and and_4 (and_4_out, not_4_out, not_5_out, register_1_q[1]);
  and and_5 (and_5_out, a, register_1_q[0], not_6_out);
  not not_6 (not_6_out, register_1_q[1]);
  Register #(.width(2)) register_1 (.D(or_2_out), .en(1'b1), .Q(register_1_q), .clk(clock_1_out), .clr(1'b0));
  or or_2 (or_2_out[0], and_1_out, and_2_out);
  or or_3 (or_2_out[1], and_3_out, and_4_out, and_5_out);
  LED X (.in(register_1_q[1]));
endmodule
