// Logisim project lab4.circ as structural Verilog: 1 circuit, main circuit main
module main (
  input  p37s,
  input  p7s,
  input  p3s,
  input  req
);

  wire and_1_out, and_2_out, and_3_out, and_4_out, and_5_out, and_6_out, and_7_out, and_8_out, and_9_out,
       clock_1_out, not_1_out, not_2_out, not_3_out, not_4_out;
  wire [1:0] or_1_out, register_1_q;

  not not_1 (not_1_out, p37s);
  not not_2 (not_2_out, p7s);
  not not_3 (not_3_out, register_1_q[0]);
  not not_4 (not_4_out, register_1_q[1]);
  Register #(.width(2)) register_1 (.D(or_1_out), .en(1'b1), .Q(register_1_q), .clk(clock_1_out), .clr(1'b0));
  Clock clock_1 (.out(clock_1_out));
  LED green (.in(and_1_out));
  and and_1 (and_1_out, not_3_out, register_1_q[1]);
  and and_2 (and_2_out, register_1_q[1], register_1_q[0]);
  LED orange (.in(and_2_out));
  LED red (.in(not_4_out));
  LED resetT (.in(and_3_out));
  and and_3 (and_3_out, not_3_out, not_4_out);
  and and_4 (and_4_out, not_2_out, register_1_q[0]);
  and and_5 (and_5_out, req, not_4_out);
  or or_1 (or_1_out[0], and_4_out, and_5_out, and_6_out);
  and and_6 (and_6_out, register_1_q[0], not_4_out);
  and and_7 (and_7_out, not_1_out, register_1_q[1]);
  and and_8 (and_8_out, p3s, register_1_q[0]);
  or or_2 (or_1_out[1], and_7_out, and_8_out, and_9_out);
  and and_9 (and_9_out, register_1_q[0], register_1_q[1]);
endmodule
