// Logisim project ControlUnit.circ as structural Verilog: 1 circuit, main circuit main
module main (
  input  p37s,
  input  p7s,
  input  p3s,
  input  req,
  input  CLK,
  input  CLR,
  output green,
  output orange,
  output red,
  output resetT
);

  wire and_4_out, and_5_out, and_6_out, and_7_out, and_8_out, and_9_out, not_1_out, not_2_out, not_3_out;
  wire [1:0] or_1_out, register_1_q;

  not not_1 (not_1_out, p37s);
  not not_2 (not_2_out, p7s);
  not not_3 (not_3_out, register_1_q[0]);
  not not_4 (red, register_1_q[1]);
  Register #(.width(2)) register_1 (.D(or_1_out), .en(1'b1), .Q(register_1_q), .clk(CLK), .clr(CLR));
  and and_1 (green, not_3_out, register_1_q[1]);
  and and_2 (orange, register_1_q[1], register_1_q[0]);
  and and_3 (resetT, not_3_out, red);
  and and_4 (and_4_out, not_2_out, register_1_q[0]);
  and and_5 (and_5_out, req, red);
  or or_1 (or_1_out[0], and_4_out, and_5_out, and_6_out);
  and and_6 (and_6_out, register_1_q[0], red);
  and and_7 (and_7_out, not_1_out, register_1_q[1]);
  and and_8 (and_8_out, p3s, register_1_q[0]);
  or or_2 (or_1_out[1], and_7_out, and_8_out, and_9_out);
  and and_9 (and_9_out, register_1_q[0], register_1_q[1]);
endmodule
