// Logisim project Datapath.circ as structural Verilog: 1 circuit, main circuit main
module main (
  input  resetT,
  input  CLK,
  output p3s,
  output p7s,
  output p37s
);

  wire [6:0] counter_1_q;

  Counter #(.width(7), .max('h7f)) counter_1 (.Q(counter_1_q), .clk(CLK), .clr(resetT));  // open: load, D, count, carry
  Comparator #(.width(7)) comparator_1 (.a(counter_1_q), .b(7'b0000110), .eq(p3s));  // open: gt, lt
  Comparator #(.width(7)) comparator_2 (.a(counter_1_q), .b(7'b0001110), .eq(p7s));  // open: gt, lt
  Comparator #(.width(7)) comparator_3 (.a(counter_1_q), .b(7'b1001010), .eq(p37s));  // open: gt, lt
endmodule
