// Logisim project main.circ as structural Verilog: 1 circuit, main circuit main
module main (
  input  req,
  input  CLR
);

  wire clock_1_out, main_1_green, main_1_orange, main_1_red, main_1_resett, main_2_p3s, main_2_p7s,
       main_2_p37s;

  Clock clock_1 (.out(clock_1_out));
  ControlUnit_main main_1 (
    .p37s(main_2_p37s), .p7s(main_2_p7s), .p3s(main_2_p3s), .req(req), .CLK(clock_1_out), .CLR(CLR),
    .green(main_1_green), .orange(main_1_orange), .red(main_1_red), .resetT(main_1_resett));
  LED led_1 (.in(main_1_red));
  Datapath_main main_2 (
    .resetT(main_1_resett), .CLK(clock_1_out), .p3s(main_2_p3s), .p7s(main_2_p7s), .p37s(main_2_p37s));
  LED led_2 (.in(main_1_green));
  LED led_3 (.in(main_1_orange));
endmodule
