// Logisim project CCode.circ as structural Verilog: 1 circuit, main circuit CCode
module CCode (
  input  goi,
  input  [7:0] x,
  input  [7:0] y,
  input  CLK,
  output [7:0] z
);

  wire main_1_ldiff, main_1_ldiff2, main_1_lxy, main_1_lz, main_1_sz_and_op, main_2_gt;

  ControlUnit_main main_1 (
    .goi(goi), .gt(main_2_gt), .CLK(CLK), .ldiff2(main_1_ldiff2), .ldiff(main_1_ldiff),
    .sz_and_op(main_1_sz_and_op), .lz(main_1_lz), .lxy(main_1_lxy));
  Datapath_main main_2 (
    .x(x), .lxy(main_1_lxy), .y(y), .sz_and_op(main_1_sz_and_op), .lz(main_1_lz), .ldiff(main_1_ldiff),
    .ldiff2(main_1_ldiff2), .CLK(CLK), .gt(main_2_gt), .z(z));
endmodule
