// Logisim project ControlUnit.circ as structural Verilog: 1 circuit, main circuit main
module main (
  input  goi,
  input  gt,
  input  CLK,
  output ldiff2,
  output ldiff,
  output sz_and_op,
  output lz,
  output lxy
);

  wire and_2_out, and_3_out, and_8_out, and_9_out, and_10_out, and_11_out, not_1_out, not_2_out, not_3_out,
       or_2_out, xor_1_out, xor_2_out, xor_3_out;
  wire [2:0] and_7_out, register_1_q;

  not not_1 (not_1_out, register_1_q[1]);
  not not_2 (not_2_out, register_1_q[2]);
  not not_3 (not_3_out, register_1_q[0]);
  Register #(.width(3)) register_1 (.D(and_7_out), .en(1'b1), .Q(register_1_q), .clk(CLK), .clr(1'b0));
  and and_1 (ldiff2, not_3_out, register_1_q[1], not_2_out);
  and and_2 (and_2_out, not_3_out, not_1_out, register_1_q[2]);
  or or_1 (ldiff, and_2_out, and_3_out);
  and and_3 (and_3_out, register_1_q[0], register_1_q[1], not_2_out);
  and and_4 (sz_and_op, not_3_out, not_1_out, register_1_q[2]);
  and and_5 (lz, not_1_out, xor_1_out);
  xor xor_1 (xor_1_out, register_1_q[0], register_1_q[2]);
  and and_6 (lxy, register_1_q[0], not_1_out, not_2_out);
  and and_7 (and_7_out[0], not_1_out, not_2_out, or_2_out);
  or or_2 (or_2_out, goi, register_1_q[0]);
  and and_8 (and_8_out, not_3_out, xor_2_out);
  xor xor_2 (xor_2_out, register_1_q[1], register_1_q[2]);
  and and_9 (and_9_out, register_1_q[0], not_2_out);
  and and_10 (and_10_out, gt, not_3_out, register_1_q[1]);
  and and_11 (and_11_out, not_3_out, xor_3_out);
  xor xor_3 (xor_3_out, register_1_q[1], register_1_q[2]);
  or or_3 (and_7_out[1], and_8_out, and_9_out);
  or or_4 (and_7_out[2], and_10_out, and_11_out);
endmodule
