// Logisim project Datapath.circ as structural Verilog: 1 circuit, main circuit main
module main (
  input  [7:0] x,
  input  lxy,
  input  [7:0] y,
  input  sz_and_op,
  input  lz,
  input  ldiff,
  input  ldiff2,
  input  CLK,
  output [7:0] z,
  output gt
);

  wire [7:0] diff2_q, diff_q, multiplexer_1_out, multiplexer_2_out, multiplexer_3_out, multiplier_1_out,
       subtractor_1_out, x_q, y_q;

  Register u_x (.D(x), .en(lxy), .Q(x_q), .clk(CLK), .clr(1'b0));
  Register u_y (.D(y), .en(lxy), .Q(y_q), .clk(CLK), .clr(1'b0));
  Register u_z (.D(multiplexer_1_out), .en(lz), .Q(z), .clk(CLK), .clr(1'b0));
  Multiplexer #(.width(8), .enable("false")) multiplexer_1 (
    .in0(8'h1), .in1(multiplier_1_out), .out(multiplexer_1_out), .sel(sz_and_op));
  Register diff (.D(subtractor_1_out), .en(ldiff), .Q(diff_q), .clk(CLK), .clr(1'b0));
  Register diff2 (.D(diff_q), .en(ldiff2), .Q(diff2_q), .clk(CLK), .clr(1'b0));
  Multiplier multiplier_1 (.a(z), .b(diff2_q), .out(multiplier_1_out));  // open: cin, cout
  Comparator comparator_1 (.a(diff_q), .b({8{1'b0}}), .gt(gt));  // open: eq, lt
  Multiplexer #(.width(8), .enable("false")) multiplexer_2 (
    .in0(x_q), .in1(diff_q), .out(multiplexer_2_out), .sel(sz_and_op));
  Multiplexer #(.width(8), .enable("false")) multiplexer_3 (
    .in0(y_q), .in1(8'h1), .out(multiplexer_3_out), .sel(sz_and_op));
  Subtractor subtractor_1 (
    .a(multiplexer_2_out), .b(multiplexer_3_out), .out(subtractor_1_out), .bin(1'b0));  // open: bout
endmodule
