// Logisim project main.circ as structural Verilog: 1 circuit, main circuit main
module main (
  input  goi,
  input  [7:0] x,
  input  [7:0] y,
  output [7:0] z
);

  wire clock_1_out;

  Clock clock_1 (.out(clock_1_out));
  CCode ccode_1 (.goi(goi), .x(x), .y(y), .CLK(clock_1_out), .z(z));
endmodule
