// Logisim project control.circ as structural Verilog: 1 circuit, main circuit control
// control-unit
module control (
  input  lsb,
  input  lt,
  input  s,
  input  CLK,
  output f_clk,
  output f_clr,
  output lo_ld,
  output hi_ld,
  output clr,
  output m_ld,
  output mux,
  output i_inc
);

  wire and_3_out, and_4_out, and_7_out, and_8_out, and_9_out, and_10_out, not_1_out, not_2_out, not_3_out;
  wire [0:0] register_1_q;
  wire [1:0] or_2_out;

  not not_1 (not_1_out, lsb);
  not not_2 (not_2_out, hi_ld);
  and and_1 (f_clk, not_3_out, hi_ld);
  and and_2 (f_clr, not_2_out, register_1_q[0]);
  and and_3 (and_3_out, s, not_3_out, not_2_out);
  and and_4 (and_4_out, register_1_q[0], hi_ld);
  and and_5 (clr, s, not_2_out, not_3_out);
  and and_6 (i_inc, hi_ld, register_1_q[0]);
  and and_7 (and_7_out, not_1_out, register_1_q[0], not_2_out);
  and and_8 (and_8_out, lt, hi_ld);
  and and_9 (and_9_out, not_3_out, hi_ld);
  and and_10 (and_10_out, s, not_3_out);
  xor xor_1 (or_2_out[1], hi_ld, register_1_q[0]);
  not not_3 (not_3_out, register_1_q[0]);
  Register #(.width(2)) register_1 (.D(or_2_out), .en(1'b1), .Q({hi_ld, register_1_q[0]}), .clk(CLK), .clr(1'b0));
  or or_1 (lo_ld, and_3_out, and_4_out);
  or or_2 (or_2_out[0], and_7_out, and_8_out, and_9_out, and_10_out);

  assign m_ld = clr;
  assign mux = i_inc;
endmodule
