// Logisim project datapath.circ as structural Verilog: 4 circuits, main circuit datapath
module datapath (
  input  [31:0] multiplicand,
  input  m_ld,
  input  hi_ld,
  input  [31:0] multiplier,
  input  mux,
  input  lo_ld,
  input  f_clk,
  input  clr,
  input  f_clr,
  input  i_inc,
  input  CLK,
  output [31:0] hi,
  output [31:0] lo,
  output lsb,
  output lt
);

  wire d_ff_1_q, i_carry, n32_bit_adder_1_cout;
  wire [31:0] m_q, multiplexer_1_out, multiplexer_2_out, n32_bit_adder_1_r, shift_right_1_bit_1_out___31_0,
       shift_right_1_bit_1_out___63_32;

  Register #(.width(32)) m (.D(multiplicand), .en(m_ld), .Q(m_q), .clk(CLK), .clr(1'b0));
  Register #(.width(32)) u_hi (.D(multiplexer_1_out), .en(hi_ld), .Q(hi), .clk(CLK), .clr(clr));
  Multiplexer #(.width(32), .enable("false")) multiplexer_1 (
    .in0(n32_bit_adder_1_r), .in1(shift_right_1_bit_1_out___63_32), .out(multiplexer_1_out), .sel(mux));
  Multiplexer #(.width(32), .enable("false")) multiplexer_2 (
    .in0(multiplier), .in1(shift_right_1_bit_1_out___31_0), .out(multiplexer_2_out), .sel(mux));
  Register #(.width(32)) u_lo (.D(multiplexer_2_out), .en(lo_ld), .Q(lo), .clk(CLK), .clr(1'b0));
  Counter #(.width(5), .max('h1f)) i (
    .load(1'b0), .count(i_inc), .carry(i_carry), .clk(CLK), .clr(1'b0));  // open: D, Q
  _32_bit_Adder u_32_bit_adder_1 (.r(n32_bit_adder_1_r), .b(hi), .a(m_q), .cout(n32_bit_adder_1_cout));
  Shift_Right_1_bit shift_right_1_bit_1 (
    .ci(d_ff_1_q), .in___63_32(hi), .in___31_0(lo), .out___63_32(shift_right_1_bit_1_out___63_32),
    .out___31_0(shift_right_1_bit_1_out___31_0));
  D_Flip_Flop d_ff_1 (
    .clk(f_clk), .D(n32_bit_adder_1_cout), .Q(d_ff_1_q), .preset(1'b0), .en(1'b1), .reset(f_clr));  // open: Qn
  not not_1 (lt, i_carry);

  assign lsb = lo[0];
endmodule

// Shifter
module Shift_Right_1_bit (
  input  [31:0] in___63_32,
  input  [31:0] in___31_0,
  input  ci,
  output [31:0] out___63_32,
  output [31:0] out___31_0
);


  assign out___31_0 = {in___63_32[0], in___31_0[31:1]};
  assign out___63_32 = {ci, in___63_32[31:1]};
endmodule

module _1_bit_Adder (
  input  ci,
  input  a,
  input  b,
  output r,
  output ci_1
);

  wire and_1_out, and_2_out, and_3_out, not_1_out, not_2_out, or_1_out, or_2_out;

  or or_1 (or_1_out, a, b);
  and and_1 (and_1_out, a, b);
  not not_1 (not_1_out, and_1_out);
  or or_2 (or_2_out, ci, and_3_out);
  and and_2 (and_2_out, ci, and_3_out);
  and and_3 (and_3_out, or_1_out, not_1_out);
  and and_4 (r, or_2_out, not_2_out);
  not not_2 (not_2_out, and_2_out);
  or or_3 (ci_1, and_2_out, and_1_out);
endmodule

// Adder
module _32_bit_Adder (
  input  [31:0] a,
  input  [31:0] b,
  output cout,
  output [31:0] r
);

  wire n1_bit_adder_2_ci_1, n1_bit_adder_3_ci_1, n1_bit_adder_4_ci_1, n1_bit_adder_5_ci_1,
       n1_bit_adder_6_ci_1, n1_bit_adder_7_ci_1, n1_bit_adder_8_ci_1, n1_bit_adder_9_ci_1,
       n1_bit_adder_10_ci_1, n1_bit_adder_11_ci_1, n1_bit_adder_12_ci_1, n1_bit_adder_13_ci_1,
       n1_bit_adder_14_ci_1, n1_bit_adder_15_ci_1, n1_bit_adder_16_ci_1, n1_bit_adder_17_ci_1,
       n1_bit_adder_18_ci_1, n1_bit_adder_19_ci_1, n1_bit_adder_20_ci_1, n1_bit_adder_21_ci_1,
       n1_bit_adder_22_ci_1, n1_bit_adder_23_ci_1, n1_bit_adder_24_ci_1, n1_bit_adder_25_ci_1,
       n1_bit_adder_26_ci_1, n1_bit_adder_27_ci_1, n1_bit_adder_28_ci_1, n1_bit_adder_29_ci_1,
       n1_bit_adder_30_ci_1, n1_bit_adder_31_ci_1, n1_bit_adder_32_ci_1;

  _1_bit_Adder u_1_bit_adder_1 (.a(a[31]), .b(b[31]), .r(r[31]), .ci_1(cout), .ci(n1_bit_adder_2_ci_1));
  _1_bit_Adder u_1_bit_adder_2 (.a(a[30]), .b(b[30]), .r(r[30]), .ci_1(n1_bit_adder_2_ci_1), .ci(n1_bit_adder_4_ci_1));
  _1_bit_Adder u_1_bit_adder_3 (.a(a[28]), .b(b[28]), .r(r[28]), .ci_1(n1_bit_adder_3_ci_1), .ci(n1_bit_adder_5_ci_1));
  _1_bit_Adder u_1_bit_adder_4 (.a(a[29]), .b(b[29]), .r(r[29]), .ci_1(n1_bit_adder_4_ci_1), .ci(n1_bit_adder_3_ci_1));
  _1_bit_Adder u_1_bit_adder_5 (.a(a[27]), .b(b[27]), .r(r[27]), .ci_1(n1_bit_adder_5_ci_1), .ci(n1_bit_adder_6_ci_1));
  _1_bit_Adder u_1_bit_adder_6 (.a(a[26]), .b(b[26]), .r(r[26]), .ci_1(n1_bit_adder_6_ci_1), .ci(n1_bit_adder_7_ci_1));
  _1_bit_Adder u_1_bit_adder_7 (.a(a[25]), .b(b[25]), .r(r[25]), .ci_1(n1_bit_adder_7_ci_1), .ci(n1_bit_adder_9_ci_1));
  _1_bit_Adder u_1_bit_adder_8 (.a(a[23]), .b(b[23]), .r(r[23]), .ci_1(n1_bit_adder_8_ci_1), .ci(n1_bit_adder_10_ci_1));
  _1_bit_Adder u_1_bit_adder_9 (.a(a[24]), .b(b[24]), .r(r[24]), .ci_1(n1_bit_adder_9_ci_1), .ci(n1_bit_adder_8_ci_1));
  _1_bit_Adder u_1_bit_adder_10 (
    .a(a[22]), .b(b[22]), .r(r[22]), .ci_1(n1_bit_adder_10_ci_1), .ci(n1_bit_adder_11_ci_1));
  _1_bit_Adder u_1_bit_adder_11 (
    .a(a[21]), .b(b[21]), .r(r[21]), .ci_1(n1_bit_adder_11_ci_1), .ci(n1_bit_adder_12_ci_1));
  _1_bit_Adder u_1_bit_adder_12 (
    .a(a[20]), .b(b[20]), .r(r[20]), .ci_1(n1_bit_adder_12_ci_1), .ci(n1_bit_adder_13_ci_1));
  _1_bit_Adder u_1_bit_adder_13 (
    .a(a[19]), .b(b[19]), .r(r[19]), .ci_1(n1_bit_adder_13_ci_1), .ci(n1_bit_adder_14_ci_1));
  _1_bit_Adder u_1_bit_adder_14 (
    .a(a[18]), .b(b[18]), .r(r[18]), .ci_1(n1_bit_adder_14_ci_1), .ci(n1_bit_adder_15_ci_1));
  _1_bit_Adder u_1_bit_adder_15 (
    .a(a[17]), .b(b[17]), .r(r[17]), .ci_1(n1_bit_adder_15_ci_1), .ci(n1_bit_adder_16_ci_1));
  _1_bit_Adder u_1_bit_adder_16 (
    .a(a[16]), .b(b[16]), .r(r[16]), .ci_1(n1_bit_adder_16_ci_1), .ci(n1_bit_adder_17_ci_1));
  _1_bit_Adder u_1_bit_adder_17 (
    .a(a[15]), .b(b[15]), .r(r[15]), .ci_1(n1_bit_adder_17_ci_1), .ci(n1_bit_adder_18_ci_1));
  _1_bit_Adder u_1_bit_adder_18 (
    .a(a[14]), .b(b[14]), .r(r[14]), .ci_1(n1_bit_adder_18_ci_1), .ci(n1_bit_adder_20_ci_1));
  _1_bit_Adder u_1_bit_adder_19 (
    .a(a[12]), .b(b[12]), .r(r[12]), .ci_1(n1_bit_adder_19_ci_1), .ci(n1_bit_adder_22_ci_1));
  _1_bit_Adder u_1_bit_adder_20 (
    .a(a[13]), .b(b[13]), .r(r[13]), .ci_1(n1_bit_adder_20_ci_1), .ci(n1_bit_adder_19_ci_1));
  _1_bit_Adder u_1_bit_adder_21 (
    .a(a[10]), .b(b[10]), .r(r[10]), .ci_1(n1_bit_adder_21_ci_1), .ci(n1_bit_adder_23_ci_1));
  _1_bit_Adder u_1_bit_adder_22 (
    .a(a[11]), .b(b[11]), .r(r[11]), .ci_1(n1_bit_adder_22_ci_1), .ci(n1_bit_adder_21_ci_1));
  _1_bit_Adder u_1_bit_adder_23 (.a(a[9]), .b(b[9]), .r(r[9]), .ci_1(n1_bit_adder_23_ci_1), .ci(n1_bit_adder_25_ci_1));
  _1_bit_Adder u_1_bit_adder_24 (.a(a[7]), .b(b[7]), .r(r[7]), .ci_1(n1_bit_adder_24_ci_1), .ci(n1_bit_adder_26_ci_1));
  _1_bit_Adder u_1_bit_adder_25 (.a(a[8]), .b(b[8]), .r(r[8]), .ci_1(n1_bit_adder_25_ci_1), .ci(n1_bit_adder_24_ci_1));
  _1_bit_Adder u_1_bit_adder_26 (.a(a[6]), .b(b[6]), .r(r[6]), .ci_1(n1_bit_adder_26_ci_1), .ci(n1_bit_adder_27_ci_1));
  _1_bit_Adder u_1_bit_adder_27 (.a(a[5]), .b(b[5]), .r(r[5]), .ci_1(n1_bit_adder_27_ci_1), .ci(n1_bit_adder_28_ci_1));
  _1_bit_Adder u_1_bit_adder_28 (.a(a[4]), .b(b[4]), .r(r[4]), .ci_1(n1_bit_adder_28_ci_1), .ci(n1_bit_adder_29_ci_1));
  _1_bit_Adder u_1_bit_adder_29 (.a(a[3]), .b(b[3]), .r(r[3]), .ci_1(n1_bit_adder_29_ci_1), .ci(n1_bit_adder_30_ci_1));
  _1_bit_Adder u_1_bit_adder_30 (.a(a[2]), .b(b[2]), .r(r[2]), .ci_1(n1_bit_adder_30_ci_1), .ci(n1_bit_adder_31_ci_1));
  _1_bit_Adder u_1_bit_adder_31 (.a(a[1]), .b(b[1]), .r(r[1]), .ci_1(n1_bit_adder_31_ci_1), .ci(n1_bit_adder_32_ci_1));
  _1_bit_Adder u_1_bit_adder_32 (.a(a[0]), .b(b[0]), .r(r[0]), .ci_1(n1_bit_adder_32_ci_1), .ci(1'b0));
endmodule
