// Logisim project mult32.circ as structural Verilog: 1 circuit, main circuit mult32
module mult32 (
  input  [31:0] multiplier,
  input  [31:0] multiplicand,
  output [31:0] res_63_32,
  output [31:0] res_31_0
);

  wire clock_1_out, control_1_clr, control_1_f_clk, control_1_f_clr, control_1_hi_ld, control_1_i_inc,
       control_1_lo_ld, control_1_m_ld, control_1_mux, datapath_1_lsb, datapath_1_lt, start_out;

  Button start (.out(start_out));
  Clock clock_1 (.out(clock_1_out));
  control control_1 (
    .lsb(datapath_1_lsb), .lt(datapath_1_lt), .s(start_out), .CLK(clock_1_out), .f_clk(control_1_f_clk),
    .f_clr(control_1_f_clr), .lo_ld(control_1_lo_ld), .hi_ld(control_1_hi_ld), .clr(control_1_clr),
    .m_ld(control_1_m_ld), .mux(control_1_mux), .i_inc(control_1_i_inc));
  datapath datapath_1 (
    .multiplicand(multiplicand), .m_ld(control_1_m_ld), .hi_ld(control_1_hi_ld), .multiplier(multiplier),
    .mux(control_1_mux), .lo_ld(control_1_lo_ld), .CLK(clock_1_out), .clr(control_1_clr), .hi(res_63_32),
    .lo(res_31_0), .lsb(datapath_1_lsb), .lt(datapath_1_lt), .f_clk(control_1_f_clk),
    .f_clr(control_1_f_clr), .i_inc(control_1_i_inc));
endmodule
